// Logisim project 4 by 2 bit RAM.circ as structural Verilog: 1 circuit, main circuit 4 by 2 bit RAM (high level)
// 4x2 RAM
module _4_by_2_bit_RAM__high_level (
  input  [3:0] Data_To_Store,
  input  Store,
  input  [1:0] Adress_to_store_at,
  output [3:0] out_4
);

  wire not_1_out;

  assign out_4 = Store ? Data_To_Store : 4'bz;  // Controlled_Buffer controlled_buffer_1
  not not_1 (not_1_out, Store);
  RAM #(.addrWidth(2), .dataWidth(4)) ram_1 (
    .addr(Adress_to_store_at), .data(out_4), .ld(not_1_out));  // open: sel, clk, clr
endmodule
