// Logisim project Calculator Full.circ as structural Verilog: 4 circuits, main circuit main
module main (
);

  wire _1_out, _2_out, _3_out, _4_out, _5_out, _6_out, _7_out, _8_out, _9_out, and_1_out, and_2_out,
       and_3_out, and_4_out, and_5_out, and_6_out, and_7_out, and_8_out,
       binary_to_digital_4_bit_0_9_carry_bit_1__0, binary_to_digital_4_bit_0_9_carry_bit_1__1,
       binary_to_digital_4_bit_0_9_carry_bit_1_out_7, binary_to_digital_4_bit_0_9_carry_bit_1_out_8,
       binary_to_digital_4_bit_0_9_carry_bit_2__0, binary_to_digital_4_bit_0_9_carry_bit_2__1,
       binary_to_digital_4_bit_0_9_carry_bit_2__9, binary_to_digital_4_bit_0_9_carry_bit_2_out_7,
       binary_to_digital_4_bit_0_9_carry_bit_2_out_8, binary_to_digital_4_bit_0_9_carry_bit_2_out_9,
       binary_to_digital_4_bit_0_9_carry_bit_2_out_10, binary_to_digital_4_bit_0_9_carry_bit_2_out_11,
       binary_to_digital_4_bit_0_9_carry_bit_2_out_12, binary_to_digital_4_bit_0_9_carry_bit_2_out_13,
       binary_to_digital_4_bit_0_9_carry_bit_3__0, binary_to_digital_4_bit_0_9_carry_bit_3__1,
       binary_to_digital_4_bit_0_9_carry_bit_3__9, binary_to_digital_4_bit_0_9_carry_bit_3_out_7,
       binary_to_digital_4_bit_0_9_carry_bit_3_out_8, binary_to_digital_4_bit_0_9_carry_bit_3_out_9,
       binary_to_digital_4_bit_0_9_carry_bit_3_out_10, binary_to_digital_4_bit_0_9_carry_bit_3_out_11,
       binary_to_digital_4_bit_0_9_carry_bit_3_out_12, binary_to_digital_4_bit_0_9_carry_bit_3_out_13,
       binary_to_digital_4_bit_0_9_carry_bit_4__0, binary_to_digital_4_bit_0_9_carry_bit_4__1,
       binary_to_digital_4_bit_0_9_carry_bit_4__9, binary_to_digital_4_bit_0_9_carry_bit_4_out_7,
       binary_to_digital_4_bit_0_9_carry_bit_4_out_8, binary_to_digital_4_bit_0_9_carry_bit_4_out_9,
       binary_to_digital_4_bit_0_9_carry_bit_4_out_10, binary_to_digital_4_bit_0_9_carry_bit_4_out_11,
       binary_to_digital_4_bit_0_9_carry_bit_4_out_12, binary_to_digital_4_bit_0_9_carry_bit_4_out_13,
       binary_to_digital_4_bit_0_9_carry_bit_5__0, binary_to_digital_4_bit_0_9_carry_bit_5__1,
       binary_to_digital_4_bit_0_9_carry_bit_5__9, binary_to_digital_4_bit_0_9_carry_bit_5_out_7,
       binary_to_digital_4_bit_0_9_carry_bit_5_out_8, binary_to_digital_4_bit_0_9_carry_bit_5_out_9,
       binary_to_digital_4_bit_0_9_carry_bit_5_out_10, binary_to_digital_4_bit_0_9_carry_bit_5_out_11,
       binary_to_digital_4_bit_0_9_carry_bit_5_out_12, binary_to_digital_4_bit_0_9_carry_bit_5_out_13,
       button_2_out, button_out, C, clock_1_out, digital_1_9_to_binary_1_out_14, display_processor_1_out_15,
       display_processor_1_out_16, display_processor_1_out_17, display_processor_1_out_18,
       display_processor_2_out_15, display_processor_2_out_16, display_processor_2_out_17,
       display_processor_2_out_18, display_processor_3_out_15, display_processor_3_out_16,
       display_processor_3_out_17, display_processor_3_out_18, display_processor_4_out_15,
       display_processor_4_out_16, display_processor_4_out_17, display_processor_4_out_18, or_1_out, X_out;
  wire [1:0] counter_1_q;
  wire [3:0] digital_1_9_to_binary_1__1_2, display_processor_1_out_14, display_processor_2_out_14,
       display_processor_3_out_14, display_processor_4_out_14, Hundreds_Place__DfB_q, Ones_Place__DfB_q,
       Tens_Place__DfB_q, Thousands_Place__DfB_q, transistor_1_out, transistor_2_out, transistor_3_out,
       transistor_4_out;

  Button button (.out(button_out));
  Button _1 (.out(_1_out));
  Button _2 (.out(_2_out));
  Button _5 (.out(_5_out));
  Button _4 (.out(_4_out));
  Button _7 (.out(_7_out));
  Button _8 (.out(_8_out));
  Button X (.out(X_out));
  Button AC (.out(C));
  Button _3 (.out(_3_out));
  Button _6 (.out(_6_out));
  Button _9 (.out(_9_out));
  Button button_2 (.out(button_2_out));
  Digital_1_9_to_Binary digital_1_9_to_binary_1 (
    ._1(_1_out), .in_2(_2_out), .in_3(_3_out), .in_4(_4_out), .in_5(_5_out), .in_6(_6_out), .in_7(_7_out),
    .in_8(_8_out), ._9(_9_out), ._1_2(digital_1_9_to_binary_1__1_2[0]), ._2(digital_1_9_to_binary_1__1_2[1]),
    ._4(digital_1_9_to_binary_1__1_2[2]), ._8(digital_1_9_to_binary_1__1_2[3]),
    .out_14(digital_1_9_to_binary_1_out_14));
  Counter #(.width(2), .max('h3)) counter_1 (
    .load(X_out), .count(button_2_out), .Q(counter_1_q), .clk(or_1_out), .clr(C));  // open: D, carry
  or or_1 (or_1_out, button_2_out, X_out);
  and and_1 (and_1_out, digital_1_9_to_binary_1_out_14, binary_to_digital_4_bit_0_9_carry_bit_1__0);
  and and_2 (and_2_out, digital_1_9_to_binary_1_out_14, binary_to_digital_4_bit_0_9_carry_bit_1__1);
  and and_3 (and_3_out, digital_1_9_to_binary_1_out_14, binary_to_digital_4_bit_0_9_carry_bit_1_out_7);
  Binary_to_Digital__4_bit___0_9___Carry_Bit binary_to_digital_4_bit_0_9_carry_bit_1 (
    ._1_8__4_bit(counter_1_q[0]), .in_2(counter_1_q[1]), .in_3(1'b0), .in_4(1'b0),
    ._0(binary_to_digital_4_bit_0_9_carry_bit_1__0), ._1(binary_to_digital_4_bit_0_9_carry_bit_1__1),
    .out_7(binary_to_digital_4_bit_0_9_carry_bit_1_out_7),
    .out_8(binary_to_digital_4_bit_0_9_carry_bit_1_out_8));  // open: out_9, out_10, out_11, out_12, out_13, _9, More_than_9
  Clock clock_1 (.out(clock_1_out));
  Register #(.width(4)) Ones_Place__DfB (
    .D(digital_1_9_to_binary_1__1_2), .Q(Ones_Place__DfB_q), .clk(and_1_out), .clr(C));  // open: en
  Register #(.width(4)) Tens_Place__DfB (
    .D(digital_1_9_to_binary_1__1_2), .Q(Tens_Place__DfB_q), .clk(and_2_out), .clr(C));  // open: en
  Register #(.width(4)) Hundreds_Place__DfB (
    .D(digital_1_9_to_binary_1__1_2), .Q(Hundreds_Place__DfB_q), .clk(and_3_out), .clr(C));  // open: en
  Register #(.width(4)) Thousands_Place__DfB (
    .D(digital_1_9_to_binary_1__1_2), .Q(Thousands_Place__DfB_q), .clk(and_4_out), .clr(C));  // open: en
  and and_4 (and_4_out, digital_1_9_to_binary_1_out_14, binary_to_digital_4_bit_0_9_carry_bit_1_out_8);
  and and_5 (and_5_out, clock_1_out, binary_to_digital_4_bit_0_9_carry_bit_1_out_8);
  Transistor #(.width(4)) transistor_1 (.in(Thousands_Place__DfB_q), .out(transistor_1_out), .gate(and_5_out));
  and and_6 (and_6_out, clock_1_out, binary_to_digital_4_bit_0_9_carry_bit_1_out_7);
  _7_Segment_Display u_7_segment_display_1 (
    .g(display_processor_1_out_14[3]), .f(display_processor_1_out_14[2]), .a(display_processor_1_out_14[1]),
    .b(display_processor_1_out_14[0]), .e(display_processor_1_out_15), .d(display_processor_1_out_16),
    .c(display_processor_1_out_17), .dp(display_processor_1_out_18));
  Display_Processor display_processor_1 (
    .in_1(binary_to_digital_4_bit_0_9_carry_bit_2__0), .in_2(binary_to_digital_4_bit_0_9_carry_bit_2__1),
    .in_3(binary_to_digital_4_bit_0_9_carry_bit_2_out_7),
    .in_4(binary_to_digital_4_bit_0_9_carry_bit_2_out_8),
    .in_5(binary_to_digital_4_bit_0_9_carry_bit_2_out_9),
    .in_6(binary_to_digital_4_bit_0_9_carry_bit_2_out_10),
    .in_7(binary_to_digital_4_bit_0_9_carry_bit_2_out_11),
    .in_8(binary_to_digital_4_bit_0_9_carry_bit_2_out_12),
    .in_9(binary_to_digital_4_bit_0_9_carry_bit_2_out_13),
    .in_10(binary_to_digital_4_bit_0_9_carry_bit_2__9), .out_15(display_processor_1_out_15),
    .out_16(display_processor_1_out_16), .out_17(display_processor_1_out_17),
    .out_18(display_processor_1_out_18), .out_11(display_processor_1_out_14[3]),
    .out_12(display_processor_1_out_14[2]), .out_13(display_processor_1_out_14[1]),
    .out_14(display_processor_1_out_14[0]));
  Binary_to_Digital__4_bit___0_9___Carry_Bit binary_to_digital_4_bit_0_9_carry_bit_2 (
    ._1_8__4_bit(transistor_1_out[0]), .in_2(transistor_1_out[1]), .in_3(transistor_1_out[2]),
    .in_4(transistor_1_out[3]), ._0(binary_to_digital_4_bit_0_9_carry_bit_2__0),
    ._1(binary_to_digital_4_bit_0_9_carry_bit_2__1), .out_7(binary_to_digital_4_bit_0_9_carry_bit_2_out_7),
    .out_8(binary_to_digital_4_bit_0_9_carry_bit_2_out_8),
    .out_9(binary_to_digital_4_bit_0_9_carry_bit_2_out_9),
    .out_10(binary_to_digital_4_bit_0_9_carry_bit_2_out_10),
    .out_11(binary_to_digital_4_bit_0_9_carry_bit_2_out_11),
    .out_12(binary_to_digital_4_bit_0_9_carry_bit_2_out_12),
    .out_13(binary_to_digital_4_bit_0_9_carry_bit_2_out_13), ._9(binary_to_digital_4_bit_0_9_carry_bit_2__9));  // open: More_than_9
  Transistor #(.width(4)) transistor_2 (.in(Hundreds_Place__DfB_q), .out(transistor_2_out), .gate(and_6_out));
  Binary_to_Digital__4_bit___0_9___Carry_Bit binary_to_digital_4_bit_0_9_carry_bit_3 (
    ._1_8__4_bit(transistor_2_out[0]), .in_2(transistor_2_out[1]), .in_3(transistor_2_out[2]),
    .in_4(transistor_2_out[3]), ._0(binary_to_digital_4_bit_0_9_carry_bit_3__0),
    ._1(binary_to_digital_4_bit_0_9_carry_bit_3__1), .out_7(binary_to_digital_4_bit_0_9_carry_bit_3_out_7),
    .out_8(binary_to_digital_4_bit_0_9_carry_bit_3_out_8),
    .out_9(binary_to_digital_4_bit_0_9_carry_bit_3_out_9),
    .out_10(binary_to_digital_4_bit_0_9_carry_bit_3_out_10),
    .out_11(binary_to_digital_4_bit_0_9_carry_bit_3_out_11),
    .out_12(binary_to_digital_4_bit_0_9_carry_bit_3_out_12),
    .out_13(binary_to_digital_4_bit_0_9_carry_bit_3_out_13), ._9(binary_to_digital_4_bit_0_9_carry_bit_3__9));  // open: More_than_9
  and and_7 (and_7_out, clock_1_out, binary_to_digital_4_bit_0_9_carry_bit_1__1);
  Transistor #(.width(4)) transistor_3 (.in(Tens_Place__DfB_q), .out(transistor_3_out), .gate(and_7_out));
  _7_Segment_Display u_7_segment_display_2 (
    .g(display_processor_2_out_14[3]), .f(display_processor_2_out_14[2]), .a(display_processor_2_out_14[1]),
    .b(display_processor_2_out_14[0]), .e(display_processor_2_out_15), .d(display_processor_2_out_16),
    .c(display_processor_2_out_17), .dp(display_processor_2_out_18));
  Display_Processor display_processor_2 (
    .in_1(binary_to_digital_4_bit_0_9_carry_bit_3__0), .in_2(binary_to_digital_4_bit_0_9_carry_bit_3__1),
    .in_3(binary_to_digital_4_bit_0_9_carry_bit_3_out_7),
    .in_4(binary_to_digital_4_bit_0_9_carry_bit_3_out_8),
    .in_5(binary_to_digital_4_bit_0_9_carry_bit_3_out_9),
    .in_6(binary_to_digital_4_bit_0_9_carry_bit_3_out_10),
    .in_7(binary_to_digital_4_bit_0_9_carry_bit_3_out_11),
    .in_8(binary_to_digital_4_bit_0_9_carry_bit_3_out_12),
    .in_9(binary_to_digital_4_bit_0_9_carry_bit_3_out_13),
    .in_10(binary_to_digital_4_bit_0_9_carry_bit_3__9), .out_15(display_processor_2_out_15),
    .out_16(display_processor_2_out_16), .out_17(display_processor_2_out_17),
    .out_18(display_processor_2_out_18), .out_11(display_processor_2_out_14[3]),
    .out_12(display_processor_2_out_14[2]), .out_13(display_processor_2_out_14[1]),
    .out_14(display_processor_2_out_14[0]));
  // _2_8_x9_bit_Full_Add 2_8_x9_bit_full_add_1: pin names not known
  _7_Segment_Display u_7_segment_display_3 (
    .g(display_processor_3_out_14[3]), .f(display_processor_3_out_14[2]), .a(display_processor_3_out_14[1]),
    .b(display_processor_3_out_14[0]), .e(display_processor_3_out_15), .d(display_processor_3_out_16),
    .c(display_processor_3_out_17), .dp(display_processor_3_out_18));
  Display_Processor display_processor_3 (
    .in_1(binary_to_digital_4_bit_0_9_carry_bit_4__0), .in_2(binary_to_digital_4_bit_0_9_carry_bit_4__1),
    .in_3(binary_to_digital_4_bit_0_9_carry_bit_4_out_7),
    .in_4(binary_to_digital_4_bit_0_9_carry_bit_4_out_8),
    .in_5(binary_to_digital_4_bit_0_9_carry_bit_4_out_9),
    .in_6(binary_to_digital_4_bit_0_9_carry_bit_4_out_10),
    .in_7(binary_to_digital_4_bit_0_9_carry_bit_4_out_11),
    .in_8(binary_to_digital_4_bit_0_9_carry_bit_4_out_12),
    .in_9(binary_to_digital_4_bit_0_9_carry_bit_4_out_13),
    .in_10(binary_to_digital_4_bit_0_9_carry_bit_4__9), .out_15(display_processor_3_out_15),
    .out_16(display_processor_3_out_16), .out_17(display_processor_3_out_17),
    .out_18(display_processor_3_out_18), .out_11(display_processor_3_out_14[3]),
    .out_12(display_processor_3_out_14[2]), .out_13(display_processor_3_out_14[1]),
    .out_14(display_processor_3_out_14[0]));
  Binary_to_Digital__4_bit___0_9___Carry_Bit binary_to_digital_4_bit_0_9_carry_bit_4 (
    ._1_8__4_bit(transistor_3_out[0]), .in_2(transistor_3_out[1]), .in_3(transistor_3_out[2]),
    .in_4(transistor_3_out[3]), ._0(binary_to_digital_4_bit_0_9_carry_bit_4__0),
    ._1(binary_to_digital_4_bit_0_9_carry_bit_4__1), .out_7(binary_to_digital_4_bit_0_9_carry_bit_4_out_7),
    .out_8(binary_to_digital_4_bit_0_9_carry_bit_4_out_8),
    .out_9(binary_to_digital_4_bit_0_9_carry_bit_4_out_9),
    .out_10(binary_to_digital_4_bit_0_9_carry_bit_4_out_10),
    .out_11(binary_to_digital_4_bit_0_9_carry_bit_4_out_11),
    .out_12(binary_to_digital_4_bit_0_9_carry_bit_4_out_12),
    .out_13(binary_to_digital_4_bit_0_9_carry_bit_4_out_13), ._9(binary_to_digital_4_bit_0_9_carry_bit_4__9));  // open: More_than_9
  and and_8 (and_8_out, clock_1_out, binary_to_digital_4_bit_0_9_carry_bit_1__0);
  Transistor #(.width(4)) transistor_4 (.in(Ones_Place__DfB_q), .out(transistor_4_out), .gate(and_8_out));
  _7_Segment_Display u_7_segment_display_4 (
    .g(display_processor_4_out_14[3]), .f(display_processor_4_out_14[2]), .a(display_processor_4_out_14[1]),
    .b(display_processor_4_out_14[0]), .e(display_processor_4_out_15), .d(display_processor_4_out_16),
    .c(display_processor_4_out_17), .dp(display_processor_4_out_18));
  Display_Processor display_processor_4 (
    .in_1(binary_to_digital_4_bit_0_9_carry_bit_5__0), .in_2(binary_to_digital_4_bit_0_9_carry_bit_5__1),
    .in_3(binary_to_digital_4_bit_0_9_carry_bit_5_out_7),
    .in_4(binary_to_digital_4_bit_0_9_carry_bit_5_out_8),
    .in_5(binary_to_digital_4_bit_0_9_carry_bit_5_out_9),
    .in_6(binary_to_digital_4_bit_0_9_carry_bit_5_out_10),
    .in_7(binary_to_digital_4_bit_0_9_carry_bit_5_out_11),
    .in_8(binary_to_digital_4_bit_0_9_carry_bit_5_out_12),
    .in_9(binary_to_digital_4_bit_0_9_carry_bit_5_out_13),
    .in_10(binary_to_digital_4_bit_0_9_carry_bit_5__9), .out_15(display_processor_4_out_15),
    .out_16(display_processor_4_out_16), .out_17(display_processor_4_out_17),
    .out_18(display_processor_4_out_18), .out_11(display_processor_4_out_14[3]),
    .out_12(display_processor_4_out_14[2]), .out_13(display_processor_4_out_14[1]),
    .out_14(display_processor_4_out_14[0]));
  Binary_to_Digital__4_bit___0_9___Carry_Bit binary_to_digital_4_bit_0_9_carry_bit_5 (
    ._1_8__4_bit(transistor_4_out[0]), .in_2(transistor_4_out[1]), .in_3(transistor_4_out[2]),
    .in_4(transistor_4_out[3]), ._0(binary_to_digital_4_bit_0_9_carry_bit_5__0),
    ._1(binary_to_digital_4_bit_0_9_carry_bit_5__1), .out_7(binary_to_digital_4_bit_0_9_carry_bit_5_out_7),
    .out_8(binary_to_digital_4_bit_0_9_carry_bit_5_out_8),
    .out_9(binary_to_digital_4_bit_0_9_carry_bit_5_out_9),
    .out_10(binary_to_digital_4_bit_0_9_carry_bit_5_out_10),
    .out_11(binary_to_digital_4_bit_0_9_carry_bit_5_out_11),
    .out_12(binary_to_digital_4_bit_0_9_carry_bit_5_out_12),
    .out_13(binary_to_digital_4_bit_0_9_carry_bit_5_out_13), ._9(binary_to_digital_4_bit_0_9_carry_bit_5__9));  // open: More_than_9
endmodule

module main___full_ram_varaint (
);

  wire _1_out, _2_out, _3_out, _4_out, _5_out, _6_out, _7_out, _8_out, _9_out, and_1_out, and_2_out,
       and_3_out, and_4_out, binary_to_digital_4_bit_0_9_carry_bit_2__0,
       binary_to_digital_4_bit_0_9_carry_bit_2__1, binary_to_digital_4_bit_0_9_carry_bit_2__9,
       binary_to_digital_4_bit_0_9_carry_bit_2_out_7, binary_to_digital_4_bit_0_9_carry_bit_2_out_8,
       binary_to_digital_4_bit_0_9_carry_bit_2_out_9, binary_to_digital_4_bit_0_9_carry_bit_2_out_10,
       binary_to_digital_4_bit_0_9_carry_bit_2_out_11, binary_to_digital_4_bit_0_9_carry_bit_2_out_12,
       binary_to_digital_4_bit_0_9_carry_bit_2_out_13, binary_to_digital_4_bit_0_9_carry_bit_3__0,
       binary_to_digital_4_bit_0_9_carry_bit_3__1, binary_to_digital_4_bit_0_9_carry_bit_3__9,
       binary_to_digital_4_bit_0_9_carry_bit_3_out_7, binary_to_digital_4_bit_0_9_carry_bit_3_out_8,
       binary_to_digital_4_bit_0_9_carry_bit_3_out_9, binary_to_digital_4_bit_0_9_carry_bit_3_out_10,
       binary_to_digital_4_bit_0_9_carry_bit_3_out_11, binary_to_digital_4_bit_0_9_carry_bit_3_out_12,
       binary_to_digital_4_bit_0_9_carry_bit_3_out_13, binary_to_digital_4_bit_0_9_carry_bit_4__0,
       binary_to_digital_4_bit_0_9_carry_bit_4__1, binary_to_digital_4_bit_0_9_carry_bit_4__9,
       binary_to_digital_4_bit_0_9_carry_bit_4_out_7, binary_to_digital_4_bit_0_9_carry_bit_4_out_8,
       binary_to_digital_4_bit_0_9_carry_bit_4_out_9, binary_to_digital_4_bit_0_9_carry_bit_4_out_10,
       binary_to_digital_4_bit_0_9_carry_bit_4_out_11, binary_to_digital_4_bit_0_9_carry_bit_4_out_12,
       binary_to_digital_4_bit_0_9_carry_bit_4_out_13, binary_to_digital_4_bit_0_9_carry_bit_5__0,
       binary_to_digital_4_bit_0_9_carry_bit_5__1, binary_to_digital_4_bit_0_9_carry_bit_5__9,
       binary_to_digital_4_bit_0_9_carry_bit_5_out_7, binary_to_digital_4_bit_0_9_carry_bit_5_out_8,
       binary_to_digital_4_bit_0_9_carry_bit_5_out_9, binary_to_digital_4_bit_0_9_carry_bit_5_out_10,
       binary_to_digital_4_bit_0_9_carry_bit_5_out_11, binary_to_digital_4_bit_0_9_carry_bit_5_out_12,
       binary_to_digital_4_bit_0_9_carry_bit_5_out_13, button_2_out, button_3_out, button_out, C,
       clock_1_out, digital_1_9_to_binary_1_out_14, display_processor_1_out_15, display_processor_1_out_16,
       display_processor_1_out_17, display_processor_1_out_18, display_processor_2_out_15,
       display_processor_2_out_16, display_processor_2_out_17, display_processor_2_out_18,
       display_processor_3_out_15, display_processor_3_out_16, display_processor_3_out_17,
       display_processor_3_out_18, display_processor_4_out_15, display_processor_4_out_16,
       display_processor_4_out_17, display_processor_4_out_18, or_1_out, or_2_out, X_out;
  wire [1:0] counter_1_q, counter_2_q;
  wire [3:0] binary_to_digital_4_bit_0_9_carry_bit_1__0, digital_1_9_to_binary_1__1_2,
       display_processor_1_out_14, display_processor_2_out_14, display_processor_3_out_14,
       display_processor_4_out_14, specialized_ram_interface_1_out_6, specialized_ram_interface_1_out_7,
       specialized_ram_interface_1_out_8, specialized_ram_interface_1_out_9, transistor_1_out,
       transistor_2_out, transistor_3_out, transistor_4_out;

  Button AC (.out(C));
  Button button (.out(button_out));
  Button button_2 (.out(button_2_out));
  Button _2 (.out(_2_out));
  Button _1 (.out(_1_out));
  Button _5 (.out(_5_out));
  Button _4 (.out(_4_out));
  Button _7 (.out(_7_out));
  Button _8 (.out(_8_out));
  Button X (.out(X_out));
  Button _3 (.out(_3_out));
  Button _6 (.out(_6_out));
  Button _9 (.out(_9_out));
  Button button_3 (.out(button_3_out));
  Digital_1_9_to_Binary digital_1_9_to_binary_1 (
    ._1(_1_out), .in_2(_2_out), .in_3(_3_out), .in_4(_4_out), .in_5(_5_out), .in_6(_6_out), .in_7(_7_out),
    .in_8(_8_out), ._9(_9_out), ._1_2(digital_1_9_to_binary_1__1_2[0]), ._2(digital_1_9_to_binary_1__1_2[1]),
    ._4(digital_1_9_to_binary_1__1_2[2]), ._8(digital_1_9_to_binary_1__1_2[3]),
    .out_14(digital_1_9_to_binary_1_out_14));
  Counter #(.width(2), .max('h3)) counter_1 (
    .load(X_out), .count(button_3_out), .Q(counter_1_q), .clk(or_1_out), .clr(C));  // open: D, carry
  or or_1 (or_1_out, button_3_out, X_out);
  Counter #(.width(2), .max('h3)) counter_2 (
    .load(button_2_out), .count(button_out), .Q(counter_2_q), .clk(or_2_out), .clr(C));  // open: D, carry
  or or_2 (or_2_out, button_out, button_2_out);
  Clock clock_1 (.out(clock_1_out));
  Specialized_RAM_Interface specialized_ram_interface_1 (
    .Value_to_Store(digital_1_9_to_binary_1__1_2), .Store(digital_1_9_to_binary_1_out_14),
    .id_of_number(counter_2_q), .Decimal_Place(counter_1_q), .Clear(C),
    .out_6(specialized_ram_interface_1_out_6), .out_7(specialized_ram_interface_1_out_7),
    .out_8(specialized_ram_interface_1_out_8), .out_9(specialized_ram_interface_1_out_9));
  Binary_to_Digital__4_bit___0_9___Carry_Bit binary_to_digital_4_bit_0_9_carry_bit_1 (
    ._1_8__4_bit(counter_1_q[0]), .in_2(counter_1_q[1]), .in_3(1'b0), .in_4(1'b0),
    ._0(binary_to_digital_4_bit_0_9_carry_bit_1__0[0]), ._1(binary_to_digital_4_bit_0_9_carry_bit_1__0[1]),
    .out_7(binary_to_digital_4_bit_0_9_carry_bit_1__0[2]),
    .out_8(binary_to_digital_4_bit_0_9_carry_bit_1__0[3]));  // open: out_9, out_10, out_11, out_12, out_13, _9, More_than_9
  and and_1 (and_1_out, clock_1_out, binary_to_digital_4_bit_0_9_carry_bit_1__0[0]);
  and and_2 (and_2_out, clock_1_out, binary_to_digital_4_bit_0_9_carry_bit_1__0[1]);
  and and_3 (and_3_out, clock_1_out, binary_to_digital_4_bit_0_9_carry_bit_1__0[2]);
  and and_4 (and_4_out, clock_1_out, binary_to_digital_4_bit_0_9_carry_bit_1__0[3]);
  Transistor #(.width(4)) transistor_1 (
    .in(specialized_ram_interface_1_out_6), .out(transistor_1_out), .gate(and_4_out));
  Transistor #(.width(4)) transistor_2 (
    .in(specialized_ram_interface_1_out_9), .out(transistor_2_out), .gate(and_1_out));
  Transistor #(.width(4)) transistor_3 (
    .in(specialized_ram_interface_1_out_8), .out(transistor_3_out), .gate(and_2_out));
  Transistor #(.width(4)) transistor_4 (
    .in(specialized_ram_interface_1_out_7), .out(transistor_4_out), .gate(and_3_out));
  _7_Segment_Display u_7_segment_display_1 (
    .g(display_processor_1_out_14[3]), .f(display_processor_1_out_14[2]), .a(display_processor_1_out_14[1]),
    .b(display_processor_1_out_14[0]), .e(display_processor_1_out_15), .d(display_processor_1_out_16),
    .c(display_processor_1_out_17), .dp(display_processor_1_out_18));
  Display_Processor display_processor_1 (
    .in_1(binary_to_digital_4_bit_0_9_carry_bit_2__0), .in_2(binary_to_digital_4_bit_0_9_carry_bit_2__1),
    .in_3(binary_to_digital_4_bit_0_9_carry_bit_2_out_7),
    .in_4(binary_to_digital_4_bit_0_9_carry_bit_2_out_8),
    .in_5(binary_to_digital_4_bit_0_9_carry_bit_2_out_9),
    .in_6(binary_to_digital_4_bit_0_9_carry_bit_2_out_10),
    .in_7(binary_to_digital_4_bit_0_9_carry_bit_2_out_11),
    .in_8(binary_to_digital_4_bit_0_9_carry_bit_2_out_12),
    .in_9(binary_to_digital_4_bit_0_9_carry_bit_2_out_13),
    .in_10(binary_to_digital_4_bit_0_9_carry_bit_2__9), .out_15(display_processor_1_out_15),
    .out_16(display_processor_1_out_16), .out_17(display_processor_1_out_17),
    .out_18(display_processor_1_out_18), .out_11(display_processor_1_out_14[3]),
    .out_12(display_processor_1_out_14[2]), .out_13(display_processor_1_out_14[1]),
    .out_14(display_processor_1_out_14[0]));
  Binary_to_Digital__4_bit___0_9___Carry_Bit binary_to_digital_4_bit_0_9_carry_bit_2 (
    ._1_8__4_bit(transistor_1_out[0]), .in_2(transistor_1_out[1]), .in_3(transistor_1_out[2]),
    .in_4(transistor_1_out[3]), ._0(binary_to_digital_4_bit_0_9_carry_bit_2__0),
    ._1(binary_to_digital_4_bit_0_9_carry_bit_2__1), .out_7(binary_to_digital_4_bit_0_9_carry_bit_2_out_7),
    .out_8(binary_to_digital_4_bit_0_9_carry_bit_2_out_8),
    .out_9(binary_to_digital_4_bit_0_9_carry_bit_2_out_9),
    .out_10(binary_to_digital_4_bit_0_9_carry_bit_2_out_10),
    .out_11(binary_to_digital_4_bit_0_9_carry_bit_2_out_11),
    .out_12(binary_to_digital_4_bit_0_9_carry_bit_2_out_12),
    .out_13(binary_to_digital_4_bit_0_9_carry_bit_2_out_13), ._9(binary_to_digital_4_bit_0_9_carry_bit_2__9));  // open: More_than_9
  Binary_to_Digital__4_bit___0_9___Carry_Bit binary_to_digital_4_bit_0_9_carry_bit_3 (
    ._1_8__4_bit(transistor_4_out[0]), .in_2(transistor_4_out[1]), .in_3(transistor_4_out[2]),
    .in_4(transistor_4_out[3]), ._0(binary_to_digital_4_bit_0_9_carry_bit_3__0),
    ._1(binary_to_digital_4_bit_0_9_carry_bit_3__1), .out_7(binary_to_digital_4_bit_0_9_carry_bit_3_out_7),
    .out_8(binary_to_digital_4_bit_0_9_carry_bit_3_out_8),
    .out_9(binary_to_digital_4_bit_0_9_carry_bit_3_out_9),
    .out_10(binary_to_digital_4_bit_0_9_carry_bit_3_out_10),
    .out_11(binary_to_digital_4_bit_0_9_carry_bit_3_out_11),
    .out_12(binary_to_digital_4_bit_0_9_carry_bit_3_out_12),
    .out_13(binary_to_digital_4_bit_0_9_carry_bit_3_out_13), ._9(binary_to_digital_4_bit_0_9_carry_bit_3__9));  // open: More_than_9
  _7_Segment_Display u_7_segment_display_2 (
    .g(display_processor_2_out_14[3]), .f(display_processor_2_out_14[2]), .a(display_processor_2_out_14[1]),
    .b(display_processor_2_out_14[0]), .e(display_processor_2_out_15), .d(display_processor_2_out_16),
    .c(display_processor_2_out_17), .dp(display_processor_2_out_18));
  Display_Processor display_processor_2 (
    .in_1(binary_to_digital_4_bit_0_9_carry_bit_3__0), .in_2(binary_to_digital_4_bit_0_9_carry_bit_3__1),
    .in_3(binary_to_digital_4_bit_0_9_carry_bit_3_out_7),
    .in_4(binary_to_digital_4_bit_0_9_carry_bit_3_out_8),
    .in_5(binary_to_digital_4_bit_0_9_carry_bit_3_out_9),
    .in_6(binary_to_digital_4_bit_0_9_carry_bit_3_out_10),
    .in_7(binary_to_digital_4_bit_0_9_carry_bit_3_out_11),
    .in_8(binary_to_digital_4_bit_0_9_carry_bit_3_out_12),
    .in_9(binary_to_digital_4_bit_0_9_carry_bit_3_out_13),
    .in_10(binary_to_digital_4_bit_0_9_carry_bit_3__9), .out_15(display_processor_2_out_15),
    .out_16(display_processor_2_out_16), .out_17(display_processor_2_out_17),
    .out_18(display_processor_2_out_18), .out_11(display_processor_2_out_14[3]),
    .out_12(display_processor_2_out_14[2]), .out_13(display_processor_2_out_14[1]),
    .out_14(display_processor_2_out_14[0]));
  _7_Segment_Display u_7_segment_display_3 (
    .g(display_processor_3_out_14[3]), .f(display_processor_3_out_14[2]), .a(display_processor_3_out_14[1]),
    .b(display_processor_3_out_14[0]), .e(display_processor_3_out_15), .d(display_processor_3_out_16),
    .c(display_processor_3_out_17), .dp(display_processor_3_out_18));
  Display_Processor display_processor_3 (
    .in_1(binary_to_digital_4_bit_0_9_carry_bit_4__0), .in_2(binary_to_digital_4_bit_0_9_carry_bit_4__1),
    .in_3(binary_to_digital_4_bit_0_9_carry_bit_4_out_7),
    .in_4(binary_to_digital_4_bit_0_9_carry_bit_4_out_8),
    .in_5(binary_to_digital_4_bit_0_9_carry_bit_4_out_9),
    .in_6(binary_to_digital_4_bit_0_9_carry_bit_4_out_10),
    .in_7(binary_to_digital_4_bit_0_9_carry_bit_4_out_11),
    .in_8(binary_to_digital_4_bit_0_9_carry_bit_4_out_12),
    .in_9(binary_to_digital_4_bit_0_9_carry_bit_4_out_13),
    .in_10(binary_to_digital_4_bit_0_9_carry_bit_4__9), .out_15(display_processor_3_out_15),
    .out_16(display_processor_3_out_16), .out_17(display_processor_3_out_17),
    .out_18(display_processor_3_out_18), .out_11(display_processor_3_out_14[3]),
    .out_12(display_processor_3_out_14[2]), .out_13(display_processor_3_out_14[1]),
    .out_14(display_processor_3_out_14[0]));
  Binary_to_Digital__4_bit___0_9___Carry_Bit binary_to_digital_4_bit_0_9_carry_bit_4 (
    ._1_8__4_bit(transistor_3_out[0]), .in_2(transistor_3_out[1]), .in_3(transistor_3_out[2]),
    .in_4(transistor_3_out[3]), ._0(binary_to_digital_4_bit_0_9_carry_bit_4__0),
    ._1(binary_to_digital_4_bit_0_9_carry_bit_4__1), .out_7(binary_to_digital_4_bit_0_9_carry_bit_4_out_7),
    .out_8(binary_to_digital_4_bit_0_9_carry_bit_4_out_8),
    .out_9(binary_to_digital_4_bit_0_9_carry_bit_4_out_9),
    .out_10(binary_to_digital_4_bit_0_9_carry_bit_4_out_10),
    .out_11(binary_to_digital_4_bit_0_9_carry_bit_4_out_11),
    .out_12(binary_to_digital_4_bit_0_9_carry_bit_4_out_12),
    .out_13(binary_to_digital_4_bit_0_9_carry_bit_4_out_13), ._9(binary_to_digital_4_bit_0_9_carry_bit_4__9));  // open: More_than_9
  _7_Segment_Display u_7_segment_display_4 (
    .g(display_processor_4_out_14[3]), .f(display_processor_4_out_14[2]), .a(display_processor_4_out_14[1]),
    .b(display_processor_4_out_14[0]), .e(display_processor_4_out_15), .d(display_processor_4_out_16),
    .c(display_processor_4_out_17), .dp(display_processor_4_out_18));
  Display_Processor display_processor_4 (
    .in_1(binary_to_digital_4_bit_0_9_carry_bit_5__0), .in_2(binary_to_digital_4_bit_0_9_carry_bit_5__1),
    .in_3(binary_to_digital_4_bit_0_9_carry_bit_5_out_7),
    .in_4(binary_to_digital_4_bit_0_9_carry_bit_5_out_8),
    .in_5(binary_to_digital_4_bit_0_9_carry_bit_5_out_9),
    .in_6(binary_to_digital_4_bit_0_9_carry_bit_5_out_10),
    .in_7(binary_to_digital_4_bit_0_9_carry_bit_5_out_11),
    .in_8(binary_to_digital_4_bit_0_9_carry_bit_5_out_12),
    .in_9(binary_to_digital_4_bit_0_9_carry_bit_5_out_13),
    .in_10(binary_to_digital_4_bit_0_9_carry_bit_5__9), .out_15(display_processor_4_out_15),
    .out_16(display_processor_4_out_16), .out_17(display_processor_4_out_17),
    .out_18(display_processor_4_out_18), .out_11(display_processor_4_out_14[3]),
    .out_12(display_processor_4_out_14[2]), .out_13(display_processor_4_out_14[1]),
    .out_14(display_processor_4_out_14[0]));
  Binary_to_Digital__4_bit___0_9___Carry_Bit binary_to_digital_4_bit_0_9_carry_bit_5 (
    ._1_8__4_bit(transistor_2_out[0]), .in_2(transistor_2_out[1]), .in_3(transistor_2_out[2]),
    .in_4(transistor_2_out[3]), ._0(binary_to_digital_4_bit_0_9_carry_bit_5__0),
    ._1(binary_to_digital_4_bit_0_9_carry_bit_5__1), .out_7(binary_to_digital_4_bit_0_9_carry_bit_5_out_7),
    .out_8(binary_to_digital_4_bit_0_9_carry_bit_5_out_8),
    .out_9(binary_to_digital_4_bit_0_9_carry_bit_5_out_9),
    .out_10(binary_to_digital_4_bit_0_9_carry_bit_5_out_10),
    .out_11(binary_to_digital_4_bit_0_9_carry_bit_5_out_11),
    .out_12(binary_to_digital_4_bit_0_9_carry_bit_5_out_12),
    .out_13(binary_to_digital_4_bit_0_9_carry_bit_5_out_13), ._9(binary_to_digital_4_bit_0_9_carry_bit_5__9));  // open: More_than_9
endmodule

module Logic_Comander (
  input  Add_Mode,
  input  Subtract_Mode,
  input  Multiply_Mode,
  input  Devide_Mode,
  input  [3:0] Data_Value_1,
  input  [3:0] Data_Value_2,
  input  Clock,
  output [8:0] out_8
);

  wire [3:0] controlled_buffer_1_out, controlled_buffer_2_out, controlled_buffer_5_out,
       controlled_buffer_6_out;
  wire [4:0] controlled_buffer_4_out, n4x5_bit_adder_1_out_3;
  wire [8:0] controlled_buffer_3_out, n2_4_x9_bit_multiplier_1_out_9;

  assign controlled_buffer_1_out = Multiply_Mode ? Data_Value_1 : 4'bz;  // Controlled_Buffer controlled_buffer_1
  assign controlled_buffer_2_out = Multiply_Mode ? Data_Value_2 : 4'bz;  // Controlled_Buffer controlled_buffer_2
  assign controlled_buffer_3_out = Multiply_Mode ? n2_4_x9_bit_multiplier_1_out_9 : 9'bz;  // Controlled_Buffer controlled_buffer_3
  _2_4_x9_bit_multiplier u_2_4_x9_bit_multiplier_1 (
    .in_1(controlled_buffer_1_out[0]), .in_2(controlled_buffer_1_out[1]), .in_3(controlled_buffer_1_out[2]),
    .in_4(controlled_buffer_1_out[3]), .in_5(controlled_buffer_2_out[0]), .in_6(controlled_buffer_2_out[1]),
    .in_7(controlled_buffer_2_out[2]), .in_8(controlled_buffer_2_out[3]),
    .out_9(n2_4_x9_bit_multiplier_1_out_9[0]), .out_10(n2_4_x9_bit_multiplier_1_out_9[1]),
    .out_11(n2_4_x9_bit_multiplier_1_out_9[2]), .out_12(n2_4_x9_bit_multiplier_1_out_9[3]),
    .out_13(n2_4_x9_bit_multiplier_1_out_9[4]), .out_14(n2_4_x9_bit_multiplier_1_out_9[5]),
    .out_15(n2_4_x9_bit_multiplier_1_out_9[6]), .out_16(n2_4_x9_bit_multiplier_1_out_9[7]),
    .out_17(n2_4_x9_bit_multiplier_1_out_9[8]));
  assign controlled_buffer_4_out = Add_Mode ? n4x5_bit_adder_1_out_3 : 5'bz;  // Controlled_Buffer controlled_buffer_4
  assign controlled_buffer_5_out = Add_Mode ? Data_Value_1 : 4'bz;  // Controlled_Buffer controlled_buffer_5
  _4x5_Bit_adder u_4x5_bit_adder_1 (
    .in_1(controlled_buffer_5_out), .in_2(controlled_buffer_6_out), .out_3(n4x5_bit_adder_1_out_3));
  assign controlled_buffer_6_out = Add_Mode ? Data_Value_2 : 4'bz;  // Controlled_Buffer controlled_buffer_6
  Controlled_Buffer #(.width(9)) controlled_buffer_7 (.out(out_8));  // open: in, en
endmodule

module _4x5_Bit_adder (
  input  [3:0] in_1,
  input  [3:0] in_2,
  output [4:0] out_3
);

  wire carry_adder_1_out_5, carry_adder_2_out_5, carry_adder_3_out_5;

  carry_adder carry_adder_1 (
    .in_1(in_1[0]), .in_2(in_2[0]), .in_3(1'b0), .out_4(out_3[0]), .out_5(carry_adder_1_out_5));
  carry_adder carry_adder_2 (
    .in_1(in_1[1]), .in_2(in_2[1]), .in_3(carry_adder_1_out_5), .out_4(out_3[1]), .out_5(carry_adder_2_out_5));
  carry_adder carry_adder_3 (
    .in_1(in_1[2]), .in_2(in_2[2]), .in_3(carry_adder_2_out_5), .out_4(out_3[2]), .out_5(carry_adder_3_out_5));
  carry_adder carry_adder_4 (
    .in_1(in_1[3]), .in_2(in_2[3]), .in_3(carry_adder_3_out_5), .out_4(out_3[3]), .out_5(out_3[4]));
endmodule
