// Logisim project Custom RAM Interface.circ as structural Verilog: 2 circuits, main circuit Specialized RAM Interface
// VSID
module Specialized_RAM_Interface (
  input  [3:0] Value_to_Store,
  input  Store,
  input  [1:0] id_of_number,
  input  [1:0] Decimal_Place,
  input  Clear,
  output [3:0] out_6,
  output [3:0] out_7,
  output [3:0] out_8,
  output [3:0] out_9
);

  wire and_1_out, and_2_out, and_3_out, and_4_out, binary_to_digital_4_bit_0_9_carry_bit_1__0,
       binary_to_digital_4_bit_0_9_carry_bit_1__1, binary_to_digital_4_bit_0_9_carry_bit_1_out_7,
       binary_to_digital_4_bit_0_9_carry_bit_1_out_8, not_1_out, or_1_out, or_2_out, or_3_out, or_4_out;
  wire [3:0] controlled_buffer_1_out, ram_1_data, ram_2_data, ram_3_data, ram_4_data;

  Binary_to_Digital__4_bit___0_9___Carry_Bit binary_to_digital_4_bit_0_9_carry_bit_1 (
    ._1_8__4_bit(Decimal_Place[0]), .in_2(Decimal_Place[1]), .in_3(1'b0), .in_4(1'b0),
    ._0(binary_to_digital_4_bit_0_9_carry_bit_1__0), ._1(binary_to_digital_4_bit_0_9_carry_bit_1__1),
    .out_7(binary_to_digital_4_bit_0_9_carry_bit_1_out_7),
    .out_8(binary_to_digital_4_bit_0_9_carry_bit_1_out_8));  // open: out_9, out_10, out_11, out_12, out_13, _9, More_than_9
  and and_1 (and_1_out, Store, binary_to_digital_4_bit_0_9_carry_bit_1__0);
  and and_2 (and_2_out, Store, binary_to_digital_4_bit_0_9_carry_bit_1__1);
  and and_3 (and_3_out, Store, binary_to_digital_4_bit_0_9_carry_bit_1_out_7);
  and and_4 (and_4_out, Store, binary_to_digital_4_bit_0_9_carry_bit_1_out_8);
  assign controlled_buffer_1_out = Store ? Value_to_Store : 4'bz;  // Controlled_Buffer controlled_buffer_1
  not not_1 (not_1_out, Store);
  or or_1 (or_1_out, not_1_out, and_1_out);
  or or_2 (or_2_out, not_1_out, and_2_out);
  or or_3 (or_3_out, not_1_out, and_3_out);
  or or_4 (or_4_out, not_1_out, and_4_out);
  RAM #(.addrWidth(2), .dataWidth(4)) ram_1 (
    .addr(id_of_number), .data(ram_1_data), .sel(or_1_out), .clk(and_1_out), .ld(not_1_out), .clr(Clear));
  RAM #(.addrWidth(2), .dataWidth(4)) ram_2 (
    .addr(id_of_number), .data(ram_2_data), .sel(or_2_out), .clk(and_2_out), .ld(not_1_out), .clr(Clear));
  RAM #(.addrWidth(2), .dataWidth(4)) ram_3 (
    .addr(id_of_number), .data(ram_3_data), .sel(or_3_out), .clk(and_3_out), .ld(not_1_out), .clr(Clear));
  RAM #(.addrWidth(2), .dataWidth(4)) ram_4 (
    .addr(id_of_number), .data(ram_4_data), .sel(or_4_out), .clk(and_4_out), .ld(not_1_out), .clr(Clear));
  assign ram_1_data = controlled_buffer_1_out;  // Buffer buffer_1, 4 bits wide
  assign ram_2_data = controlled_buffer_1_out;  // Buffer buffer_2, 4 bits wide
  assign ram_3_data = controlled_buffer_1_out;  // Buffer buffer_3, 4 bits wide
  assign ram_4_data = controlled_buffer_1_out;  // Buffer buffer_4, 4 bits wide
  assign out_6 = not_1_out ? ram_1_data : 4'bz;  // Controlled_Buffer controlled_buffer_2
  assign out_7 = not_1_out ? ram_2_data : 4'bz;  // Controlled_Buffer controlled_buffer_3
  assign out_8 = not_1_out ? ram_3_data : 4'bz;  // Controlled_Buffer controlled_buffer_4
  assign out_9 = not_1_out ? ram_4_data : 4'bz;  // Controlled_Buffer controlled_buffer_5
endmodule

module Simplified (
  input  [3:0] Value_to_Store,
  input  Store,
  input  [1:0] id_of_number,
  input  [1:0] Decimal_Place,
  input  Clear,
  output [3:0] out_6,
  output [3:0] out_7,
  output [3:0] out_8,
  output [3:0] out_9
);

  wire binary_to_digital_4_bit_0_9_carry_bit_1__0, binary_to_digital_4_bit_0_9_carry_bit_1__1,
       binary_to_digital_4_bit_0_9_carry_bit_1_out_7, binary_to_digital_4_bit_0_9_carry_bit_1_out_8, clk,
       not_1_out;

  Clock clock_1 (.out(clk));
  Binary_to_Digital__4_bit___0_9___Carry_Bit binary_to_digital_4_bit_0_9_carry_bit_1 (
    ._1_8__4_bit(Decimal_Place[0]), .in_2(Decimal_Place[1]), .in_3(1'b0), .in_4(1'b0),
    ._0(binary_to_digital_4_bit_0_9_carry_bit_1__0), ._1(binary_to_digital_4_bit_0_9_carry_bit_1__1),
    .out_7(binary_to_digital_4_bit_0_9_carry_bit_1_out_7),
    .out_8(binary_to_digital_4_bit_0_9_carry_bit_1_out_8));  // open: out_9, out_10, out_11, out_12, out_13, _9, More_than_9
  not not_1 (not_1_out, Store);
  RAM #(.addrWidth(2), .dataWidth(4), .bus("separate")) ram_1 (
    .addr(id_of_number), .din(Value_to_Store), .data(out_6), .str(Store),
    .sel(binary_to_digital_4_bit_0_9_carry_bit_1__0), .clk(clk), .ld(not_1_out), .clr(Clear));
  RAM #(.addrWidth(2), .dataWidth(4), .bus("separate")) ram_2 (
    .addr(id_of_number), .din(Value_to_Store), .data(out_7), .str(Store),
    .sel(binary_to_digital_4_bit_0_9_carry_bit_1__1), .clk(clk), .ld(not_1_out), .clr(Clear));
  RAM #(.addrWidth(2), .dataWidth(4), .bus("separate")) ram_3 (
    .addr(id_of_number), .din(Value_to_Store), .data(out_8), .str(Store),
    .sel(binary_to_digital_4_bit_0_9_carry_bit_1_out_7), .clk(clk), .ld(not_1_out), .clr(Clear));
  RAM #(.addrWidth(2), .dataWidth(4), .bus("separate")) ram_4 (
    .addr(id_of_number), .din(Value_to_Store), .data(out_9), .str(Store),
    .sel(binary_to_digital_4_bit_0_9_carry_bit_1_out_8), .clk(clk), .ld(not_1_out), .clr(Clear));
endmodule
