// Logisim project Custom RAM Interface.circ as structural Verilog: 1 circuit, main circuit Specialized RAM Interface
// VSID
module Specialized_RAM_Interface (
  input  [3:0] Value_to_Store,
  input  Store,
  input  [1:0] id_of_number,
  input  [1:0] Decimal_Place,
  input  Clear,
  output [3:0] out_6
);

  wire binary_to_digital_4_bit_0_9_carry_bit_1__0, binary_to_digital_4_bit_0_9_carry_bit_1__1,
       binary_to_digital_4_bit_0_9_carry_bit_1_out_7, binary_to_digital_4_bit_0_9_carry_bit_1_out_8,
       not_1_out;

  Binary_to_Digital__4_bit___0_9___Carry_Bit binary_to_digital_4_bit_0_9_carry_bit_1 (
    ._1_8__4_bit(Decimal_Place[0]), .in_2(Decimal_Place[1]), .in_3(1'b0), .in_4(1'b0),
    ._0(binary_to_digital_4_bit_0_9_carry_bit_1__0), ._1(binary_to_digital_4_bit_0_9_carry_bit_1__1),
    .out_7(binary_to_digital_4_bit_0_9_carry_bit_1_out_7),
    .out_8(binary_to_digital_4_bit_0_9_carry_bit_1_out_8));  // open: out_9, out_10, out_11, out_12, out_13, _9, More_than_9
  assign out_6 = Store ? Value_to_Store : 4'bz;  // Controlled_Buffer controlled_buffer_1
  not not_1 (not_1_out, Store);
  RAM #(.addrWidth(2), .dataWidth(4)) ram_1 (
    .addr(id_of_number), .data(out_6), .sel(binary_to_digital_4_bit_0_9_carry_bit_1__0), .ld(not_1_out),
    .clr(Clear));  // open: clk
  RAM #(.addrWidth(2), .dataWidth(4)) ram_2 (
    .addr(id_of_number), .sel(binary_to_digital_4_bit_0_9_carry_bit_1__1), .ld(not_1_out), .clr(Clear));  // open: data, clk
  RAM #(.addrWidth(2), .dataWidth(4)) ram_3 (
    .addr(id_of_number), .data(out_6), .sel(binary_to_digital_4_bit_0_9_carry_bit_1_out_7), .ld(not_1_out),
    .clr(Clear));  // open: clk
  RAM #(.addrWidth(2), .dataWidth(4)) ram_4 (
    .addr(id_of_number), .data(out_6), .sel(binary_to_digital_4_bit_0_9_carry_bit_1_out_8), .ld(not_1_out),
    .clr(Clear));  // open: clk
endmodule
