// Logisim project 2(4)x9 bit multiplier.circ as structural Verilog: 5 circuits, main circuit 2(4)x9 bit multiplier
module _2_4_x9_bit_multiplier (
  input  in_1,
  input  in_2,
  input  in_3,
  input  in_4,
  input  in_5,
  input  in_6,
  input  in_7,
  input  in_8,
  output out_9,
  output out_10,
  output out_11,
  output out_12,
  output out_13,
  output out_14,
  output out_15,
  output out_16,
  output out_17
);

  wire [3:0] and_1_out;
  wire [4:1] and_5_out;
  wire [5:2] and_9_out;
  wire [6:3] and_13_out;

  and and_1 (and_1_out[0], in_1, in_5);
  and and_2 (and_1_out[1], in_1, in_6);
  and and_3 (and_1_out[2], in_1, in_7);
  and and_4 (and_1_out[3], in_1, in_8);
  and and_5 (and_5_out[1], in_2, in_5);
  and and_6 (and_5_out[2], in_2, in_6);
  and and_7 (and_5_out[3], in_2, in_7);
  and and_8 (and_5_out[4], in_2, in_8);
  and and_9 (and_9_out[2], in_3, in_5);
  and and_10 (and_9_out[3], in_3, in_6);
  and and_11 (and_9_out[4], in_3, in_7);
  and and_12 (and_9_out[5], in_3, in_8);
  and and_13 (and_13_out[3], in_4, in_5);
  and and_14 (and_13_out[4], in_4, in_6);
  and and_15 (and_13_out[5], in_4, in_7);
  and and_16 (and_13_out[6], in_4, in_8);
  _4_7_x9_adder u_4_7_x9_adder_1 (
    .in_1({3'b000, and_1_out}), .in_2({2'b00, and_5_out, 1'b0}), .in_3({1'b0, and_9_out, 2'b00}),
    .in_4({and_13_out, 3'b000}),
    .out_5({out_17, out_16, out_15, out_14, out_13, out_12, out_11, out_10, out_9}));

  // Notes on the sheet:
  //   X
  //   X
  //   X
  //   X
endmodule

module carry_adder (
  input  in_1,
  input  in_2,
  input  in_3,
  output out_4,
  output out_5
);

  wire and_1_out, and_2_out, xor_1_out;

  xor xor_1 (xor_1_out, in_1, in_2);
  xor xor_2 (out_4, xor_1_out, in_3);
  and and_1 (and_1_out, xor_1_out, in_3);
  and and_2 (and_2_out, in_1, in_2);
  or or_1 (out_5, and_1_out, and_2_out);
endmodule

module _4_7_x9_adder (
  input  [6:0] in_1,
  input  [6:0] in_2,
  input  [6:0] in_3,
  input  [6:0] in_4,
  output [8:0] out_5
);

  wire [7:0] n2_7_x8_bit_1_out_3, n2_7_x8_bit_2_out_3;

  _2_7_x8_bit u_2_7_x8_bit_1 (.in_1(in_1), .in_2(in_2), .out_3(n2_7_x8_bit_1_out_3));
  _2_7_x8_bit u_2_7_x8_bit_2 (.in_1(in_3), .in_2(in_4), .out_3(n2_7_x8_bit_2_out_3));
  _2_8_x9_bit_Full_Add u_2_8_x9_bit_full_add_1 (.in_1(n2_7_x8_bit_1_out_3), .in_2(n2_7_x8_bit_2_out_3), .out_3(out_5));
endmodule

module _2_7_x8_bit (
  input  [6:0] in_1,
  input  [6:0] in_2,
  output [7:0] out_3
);

  wire carry_adder_1_out_5, carry_adder_2_out_5, carry_adder_3_out_5, carry_adder_4_out_5,
       carry_adder_5_out_5, carry_adder_6_out_5;

  carry_adder carry_adder_1 (
    .in_1(in_1[0]), .in_2(in_2[0]), .in_3(1'b0), .out_4(out_3[0]), .out_5(carry_adder_1_out_5));
  carry_adder carry_adder_2 (
    .in_1(in_1[1]), .in_2(in_2[1]), .in_3(carry_adder_1_out_5), .out_4(out_3[1]), .out_5(carry_adder_2_out_5));
  carry_adder carry_adder_3 (
    .in_1(in_1[2]), .in_2(in_2[2]), .in_3(carry_adder_2_out_5), .out_4(out_3[2]), .out_5(carry_adder_3_out_5));
  carry_adder carry_adder_4 (
    .in_1(in_1[3]), .in_2(in_2[3]), .in_3(carry_adder_3_out_5), .out_4(out_3[3]), .out_5(carry_adder_4_out_5));
  carry_adder carry_adder_5 (
    .in_1(in_1[4]), .in_2(in_2[4]), .in_3(carry_adder_4_out_5), .out_4(out_3[4]), .out_5(carry_adder_5_out_5));
  carry_adder carry_adder_6 (
    .in_1(in_1[5]), .in_2(in_2[5]), .in_3(carry_adder_5_out_5), .out_4(out_3[5]), .out_5(carry_adder_6_out_5));
  carry_adder carry_adder_7 (
    .in_1(in_1[6]), .in_2(in_2[6]), .in_3(carry_adder_6_out_5), .out_4(out_3[6]), .out_5(out_3[7]));

  // Notes on the sheet:
  //   1
  //   2
  //   4
  //   8
  //   16
  //   32
  //   64
  //   128
endmodule

module _2_8_x9_bit_Full_Add (
  input  [7:0] in_1,
  input  [7:0] in_2,
  output [8:0] out_3
);

  wire carry_adder_1_out_5, carry_adder_2_out_5, carry_adder_3_out_5, carry_adder_4_out_5,
       carry_adder_5_out_5, carry_adder_6_out_5, carry_adder_7_out_5;

  carry_adder carry_adder_1 (
    .in_1(in_1[0]), .in_2(in_2[0]), .in_3(1'b0), .out_4(out_3[0]), .out_5(carry_adder_1_out_5));
  carry_adder carry_adder_2 (
    .in_1(in_1[1]), .in_2(in_2[1]), .in_3(carry_adder_1_out_5), .out_4(out_3[1]), .out_5(carry_adder_2_out_5));
  carry_adder carry_adder_3 (
    .in_1(in_1[2]), .in_2(in_2[2]), .in_3(carry_adder_2_out_5), .out_4(out_3[2]), .out_5(carry_adder_3_out_5));
  carry_adder carry_adder_4 (
    .in_1(in_1[3]), .in_2(in_2[3]), .in_3(carry_adder_3_out_5), .out_4(out_3[3]), .out_5(carry_adder_4_out_5));
  carry_adder carry_adder_5 (
    .in_1(in_1[4]), .in_2(in_2[4]), .in_3(carry_adder_4_out_5), .out_4(out_3[4]), .out_5(carry_adder_5_out_5));
  carry_adder carry_adder_6 (
    .in_1(in_1[5]), .in_2(in_2[5]), .in_3(carry_adder_5_out_5), .out_4(out_3[5]), .out_5(carry_adder_6_out_5));
  carry_adder carry_adder_7 (
    .in_1(in_1[6]), .in_2(in_2[6]), .in_3(carry_adder_6_out_5), .out_4(out_3[6]), .out_5(carry_adder_7_out_5));
  carry_adder carry_adder_8 (
    .in_1(in_1[7]), .in_2(in_2[7]), .in_3(carry_adder_7_out_5), .out_4(out_3[7]), .out_5(out_3[8]));

  // Notes on the sheet:
  //   1
  //   2
  //   4
  //   8
  //   16
  //   32
  //   64
  //   128
endmodule
