// Logisim project 32-bit adder.circ as structural Verilog
module main (
  input  [31:0] in_1,
  input  [31:0] in_2,
  output _1,
  output _2,
  output _3,
  output _4,
  output _5,
  output _6,
  output _7,
  output _8,
  output _9,
  output _10,
  output _11,
  output _12,
  output _13,
  output _14,
  output _15,
  output _16,
  output _17,
  output _18,
  output _19,
  output _20,
  output _21,
  output _22,
  output _23,
  output _24,
  output _25,
  output _26,
  output _27,
  output _28,
  output _29,
  output _30,
  output _31,
  output _32,
  output _3_3
);

  wire _1_out_5, _2_out_5, _4_out_5, _8_2_out_5, _8_out_5, _16_2_out_5, _16_out_5, _32_2_out_5, _32_out_5,
       _64_2_out_5, _64_out_5, _128_2_out_5, _128_out_5, _256_2_out_5, _256_out_5, _512_2_out_5, _512_out_5,
       _1024_out_5, _2048_out_5, _4096_out_5, _8192_out_5, _16384_out_5, _32768_out_5, _65536_out_5,
       _131072_out_5, _262144_out_5, _524288_out_5, _1048576_out_5, _2097152_out_5, _4194304_out_5,
       _8388608_out_5;

  carry_adder u__1 (.in_1(in_1[0]), .in_2(in_2[0]), .in_3(1'b0), .out_4(_1), .out_5(_1_out_5));
  carry_adder u__2 (.in_1(in_1[1]), .in_2(in_2[1]), .in_3(_1_out_5), .out_4(_2), .out_5(_2_out_5));
  carry_adder u__4 (.in_1(in_1[2]), .in_2(in_2[2]), .in_3(_2_out_5), .out_4(_3), .out_5(_4_out_5));
  carry_adder u__8 (.in_1(in_1[3]), .in_2(in_2[3]), .in_3(_4_out_5), .out_4(_4), .out_5(_8_out_5));
  carry_adder u__16 (.in_1(in_1[4]), .in_2(in_2[4]), .in_3(_8_out_5), .out_4(_5), .out_5(_16_out_5));
  carry_adder u__32 (.in_1(in_1[5]), .in_2(in_2[5]), .in_3(_16_out_5), .out_4(_6), .out_5(_32_out_5));
  carry_adder _64 (.in_1(in_1[6]), .in_2(in_2[6]), .in_3(_32_out_5), .out_4(_7), .out_5(_64_out_5));
  carry_adder _128 (.in_1(in_1[7]), .in_2(in_2[7]), .in_3(_64_out_5), .out_4(_8), .out_5(_128_out_5));
  carry_adder _256 (.in_1(in_1[8]), .in_2(in_2[8]), .in_3(_128_out_5), .out_4(_9), .out_5(_256_out_5));
  carry_adder _512 (.in_1(in_1[9]), .in_2(in_2[9]), .in_3(_256_out_5), .out_4(_10), .out_5(_512_out_5));
  carry_adder _1024 (.in_1(in_1[10]), .in_2(in_2[10]), .in_3(_512_out_5), .out_4(_11), .out_5(_1024_out_5));
  carry_adder _2048 (.in_1(in_1[11]), .in_2(in_2[11]), .in_3(_1024_out_5), .out_4(_12), .out_5(_2048_out_5));
  carry_adder _4096 (.in_1(in_1[12]), .in_2(in_2[12]), .in_3(_2048_out_5), .out_4(_13), .out_5(_4096_out_5));
  carry_adder _8192 (.in_1(in_1[13]), .in_2(in_2[13]), .in_3(_4096_out_5), .out_4(_14), .out_5(_8192_out_5));
  carry_adder _16384 (.in_1(in_1[14]), .in_2(in_2[14]), .in_3(_8192_out_5), .out_4(_15), .out_5(_16384_out_5));
  carry_adder _32768 (.in_1(in_1[15]), .in_2(in_2[15]), .in_3(_16384_out_5), .out_4(_16), .out_5(_32768_out_5));
  carry_adder _65536 (.in_1(in_1[16]), .in_2(in_2[16]), .in_3(_32768_out_5), .out_4(_17), .out_5(_65536_out_5));
  carry_adder _131072 (.in_1(in_1[17]), .in_2(in_2[17]), .in_3(_65536_out_5), .out_4(_18), .out_5(_131072_out_5));
  carry_adder _262144 (.in_1(in_1[18]), .in_2(in_2[18]), .in_3(_131072_out_5), .out_4(_19), .out_5(_262144_out_5));
  carry_adder _524288 (.in_1(in_1[19]), .in_2(in_2[19]), .in_3(_262144_out_5), .out_4(_20), .out_5(_524288_out_5));
  carry_adder _1048576 (.in_1(in_1[20]), .in_2(in_2[20]), .in_3(_524288_out_5), .out_4(_21), .out_5(_1048576_out_5));
  carry_adder _2097152 (.in_1(in_1[21]), .in_2(in_2[21]), .in_3(_1048576_out_5), .out_4(_22), .out_5(_2097152_out_5));
  carry_adder _4194304 (.in_1(in_1[22]), .in_2(in_2[22]), .in_3(_2097152_out_5), .out_4(_23), .out_5(_4194304_out_5));
  carry_adder _8388608 (.in_1(in_1[23]), .in_2(in_2[23]), .in_3(_4194304_out_5), .out_4(_24), .out_5(_8388608_out_5));
  carry_adder _8_2 (.in_1(in_1[24]), .in_2(in_2[24]), .in_3(_8388608_out_5), .out_4(_25), .out_5(_8_2_out_5));
  carry_adder _16_2 (.in_1(in_1[25]), .in_2(in_2[25]), .in_3(_8_2_out_5), .out_4(_26), .out_5(_16_2_out_5));
  carry_adder _32_2 (.in_1(in_1[26]), .in_2(in_2[26]), .in_3(_16_2_out_5), .out_4(_27), .out_5(_32_2_out_5));
  carry_adder _64_2 (.in_1(in_1[27]), .in_2(in_2[27]), .in_3(_32_2_out_5), .out_4(_28), .out_5(_64_2_out_5));
  carry_adder _128_2 (.in_1(in_1[28]), .in_2(in_2[28]), .in_3(_64_2_out_5), .out_4(_29), .out_5(_128_2_out_5));
  carry_adder _256_2 (.in_1(in_1[29]), .in_2(in_2[29]), .in_3(_128_2_out_5), .out_4(_30), .out_5(_256_2_out_5));
  carry_adder _512_2 (.in_1(in_1[30]), .in_2(in_2[30]), .in_3(_256_2_out_5), .out_4(_31), .out_5(_512_2_out_5));
  carry_adder _1024_2 (.in_1(in_1[31]), .in_2(in_2[31]), .in_3(_512_2_out_5), .out_4(_32), .out_5(_3_3));

  // Notes on the sheet:
  //   Gave up on labels
endmodule

module carry_adder (
  input  in_1,
  input  in_2,
  input  in_3,
  output out_4,
  output out_5
);

  wire and_1_out, and_2_out, xor_1_out;

  xor xor_1 (xor_1_out, in_1, in_2);
  xor xor_2 (out_4, xor_1_out, in_3);
  and and_1 (and_1_out, xor_1_out, in_3);
  and and_2 (and_2_out, in_1, in_2);
  or or_1 (out_5, and_1_out, and_2_out);
endmodule
