// Logisim project 64-bit adder.circ as structural Verilog
module main (
  input  [31:0] in_1,
  input  [31:0] in_2,
  input  [31:0] in_3,
  input  [31:0] in_4
);

  wire _1_out_4, _1_out_5, _2_2_out_4, _2_2_out_5, _2_out_4, _2_out_5, _4_2_out_4, _4_2_out_5, _4_3_out_4,
       _4_3_out_5, _4_out_4, _4_out_5, _8_2_out_4, _8_2_out_5, _8_3_out_4, _8_3_out_5, _8_4_out_4,
       _8_4_out_5, _8_out_4, _8_out_5, _16_2_out_4, _16_2_out_5, _16_3_out_4, _16_3_out_5, _16_4_out_4,
       _16_4_out_5, _16_out_4, _16_out_5, _32_2_out_4, _32_2_out_5, _32_3_out_4, _32_3_out_5, _32_4_out_4,
       _32_4_out_5, _32_out_4, _32_out_5, _64_2_out_4, _64_2_out_5, _64_3_out_4, _64_3_out_5, _64_4_out_4,
       _64_4_out_5, _64_out_4, _64_out_5, _128_2_out_4, _128_2_out_5, _128_3_out_4, _128_3_out_5,
       _128_4_out_4, _128_4_out_5, _128_out_4, _128_out_5, _256_2_out_4, _256_2_out_5, _256_3_out_4,
       _256_3_out_5, _256_4_out_4, _256_4_out_5, _256_out_4, _256_out_5, _512_2_out_4, _512_2_out_5,
       _512_3_out_4, _512_3_out_5, _512_4_out_4, _512_4_out_5, _512_out_4, _512_out_5, _1024_2_out_4,
       _1024_2_out_5, _1024_3_out_4, _1024_3_out_5, _1024_4_out_4, _1024_4_out_5, _1024_5_out_4,
       _1024_5_out_5, _1024_out_4, _1024_out_5, _2048_2_out_4, _2048_2_out_5, _2048_out_4, _2048_out_5,
       _4096_2_out_4, _4096_2_out_5, _4096_out_4, _4096_out_5, _8192_2_out_4, _8192_2_out_5, _8192_out_4,
       _8192_out_5, _16384_2_out_4, _16384_2_out_5, _16384_out_4, _16384_out_5, _32768_2_out_4,
       _32768_2_out_5, _32768_out_4, _32768_out_5, _65536_2_out_4, _65536_2_out_5, _65536_out_4,
       _65536_out_5, _131072_2_out_4, _131072_2_out_5, _131072_out_4, _131072_out_5, _262144_2_out_4,
       _262144_2_out_5, _262144_out_4, _262144_out_5, _524288_2_out_4, _524288_2_out_5, _524288_out_4,
       _524288_out_5, _1048576_2_out_4, _1048576_2_out_5, _1048576_out_4, _1048576_out_5, _2097152_2_out_4,
       _2097152_2_out_5, _2097152_out_4, _2097152_out_5, _4194304_2_out_4, _4194304_2_out_5, _4194304_out_4,
       _4194304_out_5, _8388608_out_4, _8388608_out_5, undriven, undriven_2, undriven_3, undriven_4,
       undriven_5, undriven_6, undriven_7, undriven_8, undriven_9, undriven_10, undriven_11, undriven_12,
       undriven_13, undriven_14, undriven_15, undriven_16, undriven_17, undriven_18, undriven_19,
       undriven_20, undriven_21, undriven_22, undriven_23, undriven_24, undriven_25, undriven_26,
       undriven_27, undriven_28, undriven_29, undriven_30, undriven_31, undriven_32, undriven_33,
       undriven_34, undriven_35, undriven_36, undriven_37, undriven_38, undriven_39, undriven_40,
       undriven_41, undriven_42, undriven_43, undriven_44, undriven_45, undriven_46, undriven_47,
       undriven_48, undriven_49, undriven_50, undriven_51, undriven_52, undriven_53, undriven_54,
       undriven_55, undriven_56, undriven_57, undriven_58, undriven_59, undriven_60;

  carry_adder _1 (.in_1(in_1[0]), .in_2(in_3[0]), .in_3(1'b0), .out_4(_1_out_4), .out_5(_1_out_5));
  carry_adder _2 (.in_1(in_1[1]), .in_2(in_3[1]), .in_3(_1_out_5), .out_4(_2_out_4), .out_5(_2_out_5));
  carry_adder _4 (.in_1(in_1[2]), .in_2(in_3[2]), .in_3(_2_out_5), .out_4(_4_out_4), .out_5(_4_out_5));
  carry_adder _8 (.in_1(in_1[3]), .in_2(in_3[3]), .in_3(_4_out_5), .out_4(_8_out_4), .out_5(_8_out_5));
  carry_adder _16 (.in_1(in_1[4]), .in_2(in_3[4]), .in_3(_8_out_5), .out_4(_16_out_4), .out_5(_16_out_5));
  carry_adder _32 (.in_1(in_1[5]), .in_2(in_3[5]), .in_3(_16_out_5), .out_4(_32_out_4), .out_5(_32_out_5));
  carry_adder _64 (.in_1(in_1[6]), .in_2(in_3[6]), .in_3(_32_out_5), .out_4(_64_out_4), .out_5(_64_out_5));
  carry_adder _128 (.in_1(in_1[7]), .in_2(in_3[7]), .in_3(_64_out_5), .out_4(_128_out_4), .out_5(_128_out_5));
  carry_adder _256 (.in_1(in_1[8]), .in_2(in_3[8]), .in_3(_128_out_5), .out_4(_256_out_4), .out_5(_256_out_5));
  carry_adder _512 (.in_1(in_1[9]), .in_2(in_3[9]), .in_3(_256_out_5), .out_4(_512_out_4), .out_5(_512_out_5));
  carry_adder _1024 (.in_1(in_1[10]), .in_2(in_3[10]), .in_3(_512_out_5), .out_4(_1024_out_4), .out_5(_1024_out_5));
  carry_adder _2048 (.in_1(in_1[11]), .in_2(in_3[11]), .in_3(_1024_out_5), .out_4(_2048_out_4), .out_5(_2048_out_5));
  carry_adder _4096 (.in_1(in_1[12]), .in_2(in_3[12]), .in_3(_2048_out_5), .out_4(_4096_out_4), .out_5(_4096_out_5));
  carry_adder _8192 (.in_1(in_1[13]), .in_2(in_3[13]), .in_3(_4096_out_5), .out_4(_8192_out_4), .out_5(_8192_out_5));
  carry_adder _16384 (.in_1(in_1[14]), .in_2(in_3[14]), .in_3(_8192_out_5), .out_4(_16384_out_4), .out_5(_16384_out_5));
  carry_adder _32768 (
    .in_1(in_1[15]), .in_2(in_3[15]), .in_3(_16384_out_5), .out_4(_32768_out_4), .out_5(_32768_out_5));
  carry_adder _65536 (
    .in_1(in_1[16]), .in_2(in_3[16]), .in_3(_32768_out_5), .out_4(_65536_out_4), .out_5(_65536_out_5));
  carry_adder _131072 (
    .in_1(in_1[17]), .in_2(in_3[17]), .in_3(_65536_out_5), .out_4(_131072_out_4), .out_5(_131072_out_5));
  carry_adder _262144 (
    .in_1(in_1[18]), .in_2(in_3[18]), .in_3(_131072_out_5), .out_4(_262144_out_4), .out_5(_262144_out_5));
  carry_adder _524288 (
    .in_1(in_1[19]), .in_2(in_3[19]), .in_3(_262144_out_5), .out_4(_524288_out_4), .out_5(_524288_out_5));
  carry_adder _1048576 (
    .in_1(in_1[20]), .in_2(in_3[20]), .in_3(_524288_out_5), .out_4(_1048576_out_4), .out_5(_1048576_out_5));
  carry_adder _2097152 (
    .in_1(in_1[21]), .in_2(in_3[21]), .in_3(_1048576_out_5), .out_4(_2097152_out_4), .out_5(_2097152_out_5));
  carry_adder _4194304 (
    .in_1(in_1[22]), .in_2(in_3[22]), .in_3(_2097152_out_5), .out_4(_4194304_out_4), .out_5(_4194304_out_5));
  carry_adder _8388608 (
    .in_1(in_1[23]), .in_2(in_3[23]), .in_3(_4194304_out_5), .out_4(_8388608_out_4), .out_5(_8388608_out_5));
  carry_adder _8_2 (.in_1(in_1[24]), .in_2(in_3[24]), .in_3(_8388608_out_5), .out_4(_8_2_out_4), .out_5(_8_2_out_5));
  carry_adder _16_2 (.in_1(in_1[25]), .in_2(in_3[25]), .in_3(_8_2_out_5), .out_4(_16_2_out_4), .out_5(_16_2_out_5));
  carry_adder _32_2 (.in_1(in_1[26]), .in_2(in_3[26]), .in_3(_16_2_out_5), .out_4(_32_2_out_4), .out_5(_32_2_out_5));
  carry_adder _64_2 (.in_1(in_1[27]), .in_2(in_3[27]), .in_3(_32_2_out_5), .out_4(_64_2_out_4), .out_5(_64_2_out_5));
  carry_adder _128_2 (.in_1(in_1[28]), .in_2(in_3[28]), .in_3(_64_2_out_5), .out_4(_128_2_out_4), .out_5(_128_2_out_5));
  carry_adder _256_2 (
    .in_1(in_1[29]), .in_2(in_3[29]), .in_3(_128_2_out_5), .out_4(_256_2_out_4), .out_5(_256_2_out_5));
  carry_adder _512_2 (
    .in_1(in_1[30]), .in_2(in_3[30]), .in_3(_256_2_out_5), .out_4(_512_2_out_4), .out_5(_512_2_out_5));
  carry_adder _1024_2 (
    .in_1(in_1[31]), .in_2(in_3[31]), .in_3(_512_2_out_5), .out_4(_1024_2_out_4), .out_5(_1024_2_out_5));
  carry_adder _2_2 (.in_1(in_2[0]), .in_2(in_4[0]), .in_3(_1024_2_out_5), .out_4(_2_2_out_4), .out_5(_2_2_out_5));
  carry_adder _4_2 (.in_1(in_2[1]), .in_2(in_4[1]), .in_3(_2_2_out_5), .out_4(_4_2_out_4), .out_5(_4_2_out_5));
  carry_adder _8_3 (.in_1(undriven), .in_2(undriven_2), .in_3(_4_2_out_5), .out_4(_8_3_out_4), .out_5(_8_3_out_5));
  carry_adder _16_3 (.in_1(undriven_3), .in_2(undriven_4), .in_3(_8_3_out_5), .out_4(_16_3_out_4), .out_5(_16_3_out_5));
  carry_adder _32_3 (
    .in_1(undriven_5), .in_2(undriven_6), .in_3(_16_3_out_5), .out_4(_32_3_out_4), .out_5(_32_3_out_5));
  carry_adder _64_3 (
    .in_1(undriven_7), .in_2(undriven_8), .in_3(_32_3_out_5), .out_4(_64_3_out_4), .out_5(_64_3_out_5));
  carry_adder _128_3 (
    .in_1(undriven_9), .in_2(undriven_10), .in_3(_64_3_out_5), .out_4(_128_3_out_4), .out_5(_128_3_out_5));
  carry_adder _256_3 (
    .in_1(undriven_11), .in_2(undriven_12), .in_3(_128_3_out_5), .out_4(_256_3_out_4), .out_5(_256_3_out_5));
  carry_adder _512_3 (
    .in_1(undriven_13), .in_2(undriven_14), .in_3(_256_3_out_5), .out_4(_512_3_out_4), .out_5(_512_3_out_5));
  carry_adder _1024_3 (
    .in_1(undriven_15), .in_2(undriven_16), .in_3(_512_3_out_5), .out_4(_1024_3_out_4), .out_5(_1024_3_out_5));
  carry_adder _2048_2 (
    .in_1(undriven_17), .in_2(undriven_18), .in_3(_1024_3_out_5), .out_4(_2048_2_out_4), .out_5(_2048_2_out_5));
  carry_adder _4096_2 (
    .in_1(undriven_19), .in_2(undriven_20), .in_3(_2048_2_out_5), .out_4(_4096_2_out_4), .out_5(_4096_2_out_5));
  carry_adder _8192_2 (
    .in_1(undriven_21), .in_2(undriven_22), .in_3(_4096_2_out_5), .out_4(_8192_2_out_4), .out_5(_8192_2_out_5));
  carry_adder _16384_2 (
    .in_1(undriven_23), .in_2(undriven_24), .in_3(_8192_2_out_5), .out_4(_16384_2_out_4),
    .out_5(_16384_2_out_5));
  carry_adder _32768_2 (
    .in_1(undriven_25), .in_2(undriven_26), .in_3(_16384_2_out_5), .out_4(_32768_2_out_4),
    .out_5(_32768_2_out_5));
  carry_adder _65536_2 (
    .in_1(undriven_27), .in_2(undriven_28), .in_3(_32768_2_out_5), .out_4(_65536_2_out_4),
    .out_5(_65536_2_out_5));
  carry_adder _131072_2 (
    .in_1(undriven_29), .in_2(undriven_30), .in_3(_65536_2_out_5), .out_4(_131072_2_out_4),
    .out_5(_131072_2_out_5));
  carry_adder _262144_2 (
    .in_1(undriven_31), .in_2(undriven_32), .in_3(_131072_2_out_5), .out_4(_262144_2_out_4),
    .out_5(_262144_2_out_5));
  carry_adder _524288_2 (
    .in_1(undriven_33), .in_2(undriven_34), .in_3(_262144_2_out_5), .out_4(_524288_2_out_4),
    .out_5(_524288_2_out_5));
  carry_adder _1048576_2 (
    .in_1(undriven_35), .in_2(undriven_36), .in_3(_524288_2_out_5), .out_4(_1048576_2_out_4),
    .out_5(_1048576_2_out_5));
  carry_adder _2097152_2 (
    .in_1(undriven_37), .in_2(undriven_38), .in_3(_1048576_2_out_5), .out_4(_2097152_2_out_4),
    .out_5(_2097152_2_out_5));
  carry_adder _4194304_2 (
    .in_1(undriven_39), .in_2(undriven_40), .in_3(_2097152_2_out_5), .out_4(_4194304_2_out_4),
    .out_5(_4194304_2_out_5));
  carry_adder _4_3 (
    .in_1(undriven_41), .in_2(undriven_42), .in_3(_4194304_2_out_5), .out_4(_4_3_out_4), .out_5(_4_3_out_5));
  carry_adder _8_4 (.in_1(undriven_43), .in_2(undriven_44), .in_3(_4_3_out_5), .out_4(_8_4_out_4), .out_5(_8_4_out_5));
  carry_adder _16_4 (
    .in_1(undriven_45), .in_2(undriven_46), .in_3(_8_4_out_5), .out_4(_16_4_out_4), .out_5(_16_4_out_5));
  carry_adder _32_4 (
    .in_1(undriven_47), .in_2(undriven_48), .in_3(_16_4_out_5), .out_4(_32_4_out_4), .out_5(_32_4_out_5));
  carry_adder _64_4 (
    .in_1(undriven_49), .in_2(undriven_50), .in_3(_32_4_out_5), .out_4(_64_4_out_4), .out_5(_64_4_out_5));
  carry_adder _128_4 (
    .in_1(undriven_51), .in_2(undriven_52), .in_3(_64_4_out_5), .out_4(_128_4_out_4), .out_5(_128_4_out_5));
  carry_adder _256_4 (
    .in_1(undriven_53), .in_2(undriven_54), .in_3(_128_4_out_5), .out_4(_256_4_out_4), .out_5(_256_4_out_5));
  carry_adder _512_4 (
    .in_1(undriven_55), .in_2(undriven_56), .in_3(_256_4_out_5), .out_4(_512_4_out_4), .out_5(_512_4_out_5));
  carry_adder _1024_4 (
    .in_1(undriven_57), .in_2(undriven_58), .in_3(_512_4_out_5), .out_4(_1024_4_out_4), .out_5(_1024_4_out_5));
  carry_adder _1024_5 (
    .in_1(undriven_59), .in_2(undriven_60), .in_3(_1024_4_out_5), .out_4(_1024_5_out_4), .out_5(_1024_5_out_5));

  // Notes on the sheet:
  //   1
  //   2
  //   3
  //   4
  //   5
  //   6
  //   7
  //   8
  //   9
  //   10
  //   11
  //   12
  //   13
  //   14
  //   15
  //   16
  //   17
  //   18
  //   19
  //   20
  //   21
  //   22
  //   23
  //   24
  //   25
  //   26
  //   27
  //   28
  //   29
  //   30
  //   31
  //   32
  //   33
  //   34
  //   35
  //   36
  //   37
  //   38
  //   39
  //   40
  //   41
  //   42
  //   43
  //   44
  //   45
  //   46
  //   47
  //   48
  //   49
  //   50
  //   51
  //   52
  //   53
  //   54
  //   55
  //   56
  //   57
  //   58
  //   59
  //   60
  //   61
  //   62
  //   63
  //   64
  //   Gave up on labels
  //   65
endmodule

module carry_adder (
  input  in_1,
  input  in_2,
  input  in_3,
  output out_4,
  output out_5
);

  wire and_1_out, and_2_out, xor_1_out;

  xor xor_1 (xor_1_out, in_1, in_2);
  xor xor_2 (out_4, xor_1_out, in_3);
  and and_1 (and_1_out, xor_1_out, in_3);
  and and_2 (and_2_out, in_1, in_2);
  or or_1 (out_5, and_1_out, and_2_out);
endmodule
