// Logisim project Calculator.circ as structural Verilog: 11 circuits, main circuit main
module main (
  input  in_1,
  input  in_2,
  input  in_3,
  input  in_4,
  input  in_5
);

  wire _1_out, _2_out, _3_out, _4_out, _5_out, _6_out, _7_out, _8_out, _9_out, AC_out,
       binary_to_digital_4_bit_0_9_carry_bit_1__0, binary_to_digital_4_bit_0_9_carry_bit_1__1,
       binary_to_digital_4_bit_0_9_carry_bit_1__9, binary_to_digital_4_bit_0_9_carry_bit_1_out_7,
       binary_to_digital_4_bit_0_9_carry_bit_1_out_8, binary_to_digital_4_bit_0_9_carry_bit_1_out_9,
       binary_to_digital_4_bit_0_9_carry_bit_1_out_10, binary_to_digital_4_bit_0_9_carry_bit_1_out_11,
       binary_to_digital_4_bit_0_9_carry_bit_1_out_12, binary_to_digital_4_bit_0_9_carry_bit_1_out_13,
       button_out, digital_1_9_to_binary_1__1_2, digital_1_9_to_binary_1__2, digital_1_9_to_binary_1__4,
       digital_1_9_to_binary_1__8, display_processor_1_out_11, display_processor_1_out_12,
       display_processor_1_out_13, display_processor_1_out_14, display_processor_1_out_15,
       display_processor_1_out_16, display_processor_1_out_17, display_processor_1_out_18,
       n1_bit_holder_1_out_3, RAM_out_11, RAM_out_12, RAM_out_13, RAM_out_14, vertical_flip_1_out_10,
       vertical_flip_1_out_11, vertical_flip_1_out_12, vertical_flip_1_out_13, vertical_flip_1_out_14,
       vertical_flip_1_out_15, vertical_flip_1_out_16, vertical_flip_1_out_17, vertical_flip_1_out_18;

  Button AC (.out(AC_out));
  Button _8 (.out(_8_out));
  Button _7 (.out(_7_out));
  Button _4 (.out(_4_out));
  Button _5 (.out(_5_out));
  Button _2 (.out(_2_out));
  Button _1 (.out(_1_out));
  Button _0 ();  // open: out
  Button _9 (.out(_9_out));
  Button _6 (.out(_6_out));
  Button _3 (.out(_3_out));
  Button button (.out(button_out));
  Vertical_Flip vertical_flip_1 (
    .in_1(_9_out), .in_2(_8_out), .in_3(_7_out), .in_4(_6_out), .in_5(_5_out), .in_6(_4_out), .in_7(_3_out),
    .in_8(_2_out), .in_9(_1_out), .out_10(vertical_flip_1_out_10), .out_11(vertical_flip_1_out_11),
    .out_12(vertical_flip_1_out_12), .out_13(vertical_flip_1_out_13), .out_14(vertical_flip_1_out_14),
    .out_15(vertical_flip_1_out_15), .out_16(vertical_flip_1_out_16), .out_17(vertical_flip_1_out_17),
    .out_18(vertical_flip_1_out_18));
  Digital_1_9_to_Binary digital_1_9_to_binary_1 (
    ._1(vertical_flip_1_out_10), .in_2(vertical_flip_1_out_11), .in_3(vertical_flip_1_out_12),
    .in_4(vertical_flip_1_out_13), .in_5(vertical_flip_1_out_14), .in_6(vertical_flip_1_out_15),
    .in_7(vertical_flip_1_out_16), .in_8(vertical_flip_1_out_17), ._9(vertical_flip_1_out_18),
    ._1_2(digital_1_9_to_binary_1__1_2), ._2(digital_1_9_to_binary_1__2), ._4(digital_1_9_to_binary_1__4),
    ._8(digital_1_9_to_binary_1__8));  // open: out_14
  _1_Bit_Holder u_1_bit_holder_1 (.Set(AC_out), .Reset(button_out), .out_3(n1_bit_holder_1_out_3));
  Addressable_RAM RAM (
    .Read(in_1), .Set(n1_bit_holder_1_out_3), .Address(in_2), .in_4(in_3), .in_5(in_4), .in_6(in_5),
    .Sets(digital_1_9_to_binary_1__1_2), .in_8(digital_1_9_to_binary_1__2),
    .in_9(digital_1_9_to_binary_1__4), .in_10(digital_1_9_to_binary_1__8), .out_11(RAM_out_11),
    .out_12(RAM_out_12), .out_13(RAM_out_13), .out_14(RAM_out_14));
  _7_Segment_Display u_7_segment_display_1 (
    .g(display_processor_1_out_11), .f(display_processor_1_out_12), .a(display_processor_1_out_13),
    .b(display_processor_1_out_14), .e(display_processor_1_out_15), .d(display_processor_1_out_16),
    .c(display_processor_1_out_17), .dp(display_processor_1_out_18));
  Display_Processor display_processor_1 (
    .in_1(binary_to_digital_4_bit_0_9_carry_bit_1__0), .in_2(binary_to_digital_4_bit_0_9_carry_bit_1__1),
    .in_3(binary_to_digital_4_bit_0_9_carry_bit_1_out_7),
    .in_4(binary_to_digital_4_bit_0_9_carry_bit_1_out_8),
    .in_5(binary_to_digital_4_bit_0_9_carry_bit_1_out_9),
    .in_6(binary_to_digital_4_bit_0_9_carry_bit_1_out_10),
    .in_7(binary_to_digital_4_bit_0_9_carry_bit_1_out_11),
    .in_8(binary_to_digital_4_bit_0_9_carry_bit_1_out_12),
    .in_9(binary_to_digital_4_bit_0_9_carry_bit_1_out_13),
    .in_10(binary_to_digital_4_bit_0_9_carry_bit_1__9), .out_15(display_processor_1_out_15),
    .out_16(display_processor_1_out_16), .out_17(display_processor_1_out_17),
    .out_18(display_processor_1_out_18), .out_11(display_processor_1_out_11),
    .out_12(display_processor_1_out_12), .out_13(display_processor_1_out_13),
    .out_14(display_processor_1_out_14));
  Binary_to_Digital__4_bit___0_9___Carry_Bit binary_to_digital_4_bit_0_9_carry_bit_1 (
    ._1_8__4_bit(digital_1_9_to_binary_1__1_2), .in_2(digital_1_9_to_binary_1__2),
    .in_3(digital_1_9_to_binary_1__4), .in_4(digital_1_9_to_binary_1__8),
    ._0(binary_to_digital_4_bit_0_9_carry_bit_1__0), ._1(binary_to_digital_4_bit_0_9_carry_bit_1__1),
    .out_7(binary_to_digital_4_bit_0_9_carry_bit_1_out_7),
    .out_8(binary_to_digital_4_bit_0_9_carry_bit_1_out_8),
    .out_9(binary_to_digital_4_bit_0_9_carry_bit_1_out_9),
    .out_10(binary_to_digital_4_bit_0_9_carry_bit_1_out_10),
    .out_11(binary_to_digital_4_bit_0_9_carry_bit_1_out_11),
    .out_12(binary_to_digital_4_bit_0_9_carry_bit_1_out_12),
    .out_13(binary_to_digital_4_bit_0_9_carry_bit_1_out_13), ._9(binary_to_digital_4_bit_0_9_carry_bit_1__9));  // open: More_than_9

  // Notes on the sheet:
  //   Press To Turn On
  //   789
  //   456
  //   123
  //   Decimal To Binary
endmodule

module Digital_1_9_to_Binary (
  input  _1,
  input  in_2,
  input  in_3,
  input  in_4,
  input  in_5,
  input  in_6,
  input  in_7,
  input  in_8,
  input  _9,
  output _1_2,
  output _2,
  output _4,
  output _8,
  output out_14
);

  or or_1 (_1_2, _1, in_3, in_5, _9, in_7);
  or or_2 (_2, in_2, in_3, in_7, in_6);
  or or_3 (_4, in_4, in_5, in_6, in_7);
  or or_4 (_8, in_8, _9);
  or or_5 (out_14, _1_2, _2, _4, _8);

  // Notes on the sheet:
  //   Anything Was Input
endmodule

module Vertical_Flip (
  input  in_1,
  input  in_2,
  input  in_3,
  input  in_4,
  input  in_5,
  input  in_6,
  input  in_7,
  input  in_8,
  input  in_9,
  output out_10,
  output out_11,
  output out_12,
  output out_13,
  output out_14,
  output out_15,
  output out_16,
  output out_17,
  output out_18
);


  assign out_10 = in_9;
  assign out_11 = in_8;
  assign out_12 = in_7;
  assign out_13 = in_6;
  assign out_14 = in_5;
  assign out_15 = in_4;
  assign out_16 = in_3;
  assign out_17 = in_2;
  assign out_18 = in_1;
endmodule

module Half_Adder (
  input  in_1,
  input  in_2,
  output _1,
  output _2
);

  xor xor_1 (_1, in_1, in_2);
  and and_1 (_2, in_1, in_2);
endmodule

module _1_Bit_Holder (
  input  Set,
  input  Reset,
  output out_3
);

  wire nor_1_out, nor_2_out;

  D_Flip_Flop d_ff_1 (.Q(out_3), .preset(Set), .reset(Reset));  // open: clk, D, Qn, en
  nor nor_1 (nor_1_out, Set, nor_2_out);
  nor nor_2 (nor_2_out, nor_1_out, Reset);
endmodule

// RS-A-S
module Addressable_RAM (
  input  Read,
  input  Set,
  input  Address,
  input  in_4,
  input  in_5,
  input  in_6,
  input  Sets,
  input  in_8,
  input  in_9,
  input  in_10,
  output out_11,
  output out_12,
  output out_13,
  output out_14
);

  wire _0001_out, _0010_out, _0100_out, _1000_out, and_1_out, and_2_out, and_3_out, and_4_out, and_5_out,
       and_6_out, and_7_out, and_8_out, binary_to_digital_4_bit_0_9_carry_bit_1__1,
       binary_to_digital_4_bit_0_9_carry_bit_1_out_7, binary_to_digital_4_bit_0_9_carry_bit_1_out_8,
       binary_to_digital_4_bit_0_9_carry_bit_1_out_9, or_1_out, readable_4_bit_raw_register_1_out_7,
       readable_4_bit_raw_register_1_out_8, readable_4_bit_raw_register_1_out_9,
       readable_4_bit_raw_register_1_out_10, readable_4_bit_raw_register_2_out_7,
       readable_4_bit_raw_register_2_out_9, readable_4_bit_raw_register_2_out_10,
       readable_4_bit_raw_register_3_out_7, readable_4_bit_raw_register_3_out_8,
       readable_4_bit_raw_register_3_out_9, readable_4_bit_raw_register_3_out_10,
       readable_4_bit_raw_register_4_out_7, readable_4_bit_raw_register_4_out_8,
       readable_4_bit_raw_register_4_out_9, readable_4_bit_raw_register_4_out_10;

  or or_1 (or_1_out, Read, Set);
  and _0001 (_0001_out, or_1_out, Address);
  and _0010 (_0010_out, or_1_out, in_4);
  and _0100 (_0100_out, or_1_out, in_5);
  and _1000 (_1000_out, or_1_out, in_6);
  Binary_to_Digital__4_bit___0_9___Carry_Bit binary_to_digital_4_bit_0_9_carry_bit_1 (
    ._1_8__4_bit(_0001_out), .in_2(_0010_out), .in_3(_0100_out), .in_4(_1000_out),
    ._1(binary_to_digital_4_bit_0_9_carry_bit_1__1), .out_7(binary_to_digital_4_bit_0_9_carry_bit_1_out_7),
    .out_8(binary_to_digital_4_bit_0_9_carry_bit_1_out_8),
    .out_9(binary_to_digital_4_bit_0_9_carry_bit_1_out_9));  // open: _0, out_10, out_11, out_12, out_13, _9, More_than_9
  and and_1 (and_1_out, binary_to_digital_4_bit_0_9_carry_bit_1__1, Read);
  and and_2 (and_2_out, binary_to_digital_4_bit_0_9_carry_bit_1__1, Set);
  and and_3 (and_3_out, binary_to_digital_4_bit_0_9_carry_bit_1_out_7, Read);
  and and_4 (and_4_out, binary_to_digital_4_bit_0_9_carry_bit_1_out_7, Set);
  and and_5 (and_5_out, binary_to_digital_4_bit_0_9_carry_bit_1_out_8, Read);
  and and_6 (and_6_out, binary_to_digital_4_bit_0_9_carry_bit_1_out_8, Set);
  and and_7 (and_7_out, binary_to_digital_4_bit_0_9_carry_bit_1_out_9, Read);
  and and_8 (and_8_out, binary_to_digital_4_bit_0_9_carry_bit_1_out_9, Set);
  Readable_4_bit_Raw_Register readable_4_bit_raw_register_1 (
    .Read(and_1_out), .Set(and_2_out), .Sets__4_bit(Sets), .in_4(in_8), .in_5(in_9), .in_6(in_10),
    .out_7(readable_4_bit_raw_register_1_out_7), .out_8(readable_4_bit_raw_register_1_out_8),
    .out_9(readable_4_bit_raw_register_1_out_9), .out_10(readable_4_bit_raw_register_1_out_10));
  Readable_4_bit_Raw_Register readable_4_bit_raw_register_2 (
    .Read(and_3_out), .Set(and_4_out), .Sets__4_bit(Sets), .in_4(in_8), .in_5(in_9), .in_6(in_10),
    .out_7(readable_4_bit_raw_register_2_out_7), .out_8(readable_4_bit_raw_register_1_out_9),
    .out_9(readable_4_bit_raw_register_2_out_9), .out_10(readable_4_bit_raw_register_2_out_10));
  Readable_4_bit_Raw_Register readable_4_bit_raw_register_3 (
    .Read(and_5_out), .Set(and_6_out), .Sets__4_bit(Sets), .in_4(in_8), .in_5(in_9), .in_6(in_10),
    .out_7(readable_4_bit_raw_register_3_out_7), .out_8(readable_4_bit_raw_register_3_out_8),
    .out_9(readable_4_bit_raw_register_3_out_9), .out_10(readable_4_bit_raw_register_3_out_10));
  Readable_4_bit_Raw_Register readable_4_bit_raw_register_4 (
    .Read(and_7_out), .Set(and_8_out), .Sets__4_bit(Sets), .in_4(in_8), .in_5(in_9), .in_6(in_10),
    .out_7(readable_4_bit_raw_register_4_out_7), .out_8(readable_4_bit_raw_register_4_out_8),
    .out_9(readable_4_bit_raw_register_4_out_9), .out_10(readable_4_bit_raw_register_4_out_10));
  or or_2 (out_11, readable_4_bit_raw_register_1_out_7, readable_4_bit_raw_register_2_out_7, readable_4_bit_raw_register_3_out_7, readable_4_bit_raw_register_4_out_7);
  or or_3 (out_12, readable_4_bit_raw_register_1_out_8, readable_4_bit_raw_register_1_out_9, readable_4_bit_raw_register_3_out_8, readable_4_bit_raw_register_4_out_8);
  or or_4 (out_13, readable_4_bit_raw_register_1_out_9, readable_4_bit_raw_register_2_out_9, readable_4_bit_raw_register_3_out_9, readable_4_bit_raw_register_4_out_9);
  or or_5 (out_14, readable_4_bit_raw_register_1_out_10, readable_4_bit_raw_register_2_out_10, readable_4_bit_raw_register_3_out_10, readable_4_bit_raw_register_4_out_10);
endmodule

// RSB
module Readable_4_bit_Raw_Register (
  input  Read,
  input  Set,
  input  Sets__4_bit,
  input  in_4,
  input  in_5,
  input  in_6,
  output out_7,
  output out_8,
  output out_9,
  output out_10
);

  wire and_1_out, and_2_out, and_3_out, and_4_out, and_5_out, and_6_out, and_7_out, and_8_out,
       n1_bit_holder_1_out_3, n1_bit_holder_2_out_3, n1_bit_holder_3_out_3, n1_bit_holder_4_out_3, not_1_out,
       not_2_out, not_3_out, not_4_out;

  not not_1 (not_1_out, Sets__4_bit);
  not not_2 (not_2_out, in_4);
  not not_3 (not_3_out, in_5);
  not not_4 (not_4_out, in_6);
  and and_1 (and_1_out, Sets__4_bit, Set);
  and and_2 (and_2_out, not_1_out, Set);
  and and_3 (and_3_out, in_4, Set);
  and and_4 (and_4_out, not_2_out, Set);
  and and_5 (and_5_out, in_5, Set);
  and and_6 (and_6_out, not_3_out, Set);
  and and_7 (and_7_out, in_6, Set);
  and and_8 (and_8_out, not_4_out, Set);
  _1_Bit_Holder u_1_bit_holder_1 (.Set(and_1_out), .Reset(and_2_out), .out_3(n1_bit_holder_1_out_3));
  _1_Bit_Holder u_1_bit_holder_2 (.Set(and_3_out), .Reset(and_4_out), .out_3(n1_bit_holder_2_out_3));
  _1_Bit_Holder u_1_bit_holder_3 (.Set(and_5_out), .Reset(and_6_out), .out_3(n1_bit_holder_3_out_3));
  _1_Bit_Holder u_1_bit_holder_4 (.Set(and_7_out), .Reset(and_8_out), .out_3(n1_bit_holder_4_out_3));
  and and_9 (out_7, n1_bit_holder_1_out_3, Read);
  and and_10 (out_8, n1_bit_holder_2_out_3, Read);
  and and_11 (out_9, n1_bit_holder_3_out_3, Read);
  and and_12 (out_10, n1_bit_holder_4_out_3, Read);

  // Notes on the sheet:
  //   Top (1) down (8)
endmodule

module Binary_to_Digital__4_bit___0_9___Carry_Bit (
  input  _1_8__4_bit,
  input  in_2,
  input  in_3,
  input  in_4,
  output _0,
  output _1,
  output out_7,
  output out_8,
  output out_9,
  output out_10,
  output out_11,
  output out_12,
  output out_13,
  output _9,
  output More_than_9
);

  wire not_1_out, not_2_out, not_3_out, not_4_out, not_5_out, not_6_out, not_7_out, not_8_out, not_9_out,
       not_10_out, not_11_out, not_12_out, not_13_out, not_14_out, not_15_out, not_16_out, not_17_out,
       not_18_out, not_19_out, not_20_out, not_21_out;

  not not_1 (not_1_out, in_2);
  not not_2 (not_2_out, in_3);
  not not_3 (not_3_out, in_4);
  not not_4 (not_4_out, _1_8__4_bit);
  not not_5 (not_5_out, in_3);
  not not_6 (not_6_out, in_4);
  not not_7 (not_7_out, in_3);
  not not_8 (not_8_out, in_4);
  not not_9 (not_9_out, _1_8__4_bit);
  not not_10 (not_10_out, in_2);
  not not_11 (not_11_out, in_4);
  not not_12 (not_12_out, in_2);
  not not_13 (not_13_out, in_4);
  not not_14 (not_14_out, _1_8__4_bit);
  not not_15 (not_15_out, in_4);
  not not_16 (not_16_out, in_4);
  not not_17 (not_17_out, _1_8__4_bit);
  not not_18 (not_18_out, in_2);
  not not_19 (not_19_out, in_3);
  not not_20 (not_20_out, in_2);
  not not_21 (not_21_out, in_3);
  nor nor_1 (_0, _1_8__4_bit, in_2, in_3, in_4);
  and and_1 (_1, _1_8__4_bit, not_1_out, not_2_out, not_3_out);
  and and_2 (out_7, not_4_out, in_2, not_5_out, not_6_out);
  and and_3 (out_8, _1_8__4_bit, in_2, not_7_out, not_8_out);
  and and_4 (out_9, not_9_out, not_10_out, in_3, not_11_out);
  and and_5 (out_10, _1_8__4_bit, not_12_out, in_3, not_13_out);
  and and_6 (out_11, not_14_out, in_2, in_3, not_15_out);
  and and_7 (out_12, _1_8__4_bit, in_2, in_3, not_16_out);
  and and_8 (out_13, not_17_out, not_18_out, not_19_out, in_4);
  and and_9 (_9, _1_8__4_bit, not_20_out, not_21_out, in_4);
  nor nor_2 (More_than_9, _0, _1, out_7, out_8, out_9, out_10, out_11, out_12, out_13, _9);

  // Notes on the sheet:
  //   0-9 Top Down
endmodule

module Display_Processor (
  input  in_1,
  input  in_2,
  input  in_3,
  input  in_4,
  input  in_5,
  input  in_6,
  input  in_7,
  input  in_8,
  input  in_9,
  input  in_10,
  output out_11,
  output out_12,
  output out_13,
  output out_14,
  output out_15,
  output out_16,
  output out_17,
  output out_18
);

  or or_1 (out_11, in_10, in_3, in_4, in_5, in_6, in_7, in_9);
  or or_2 (out_15, in_1, in_3, in_9, in_7);
  or or_3 (out_12, in_10, in_1, in_5, in_7, in_9, in_6);
  _7_Segment_Display u_7_segment_display_1 (
    .g(out_11), .f(out_12), .a(out_13), .b(out_14), .e(out_15), .d(out_16), .c(out_17), .dp(1'b0));
  or or_4 (out_16, in_9, in_1, in_3, in_4, in_6, in_7, in_10);
  or or_5 (out_13, in_10, in_9, in_1, in_3, in_6, in_7, in_8, in_4);
  or or_6 (out_17, in_9, in_8, in_1, in_2, in_4, in_5, in_6, in_7, in_10);
  or or_7 (out_14, in_9, in_1, in_2, in_3, in_5, in_8, in_4, in_10);

  assign out_18 = 1'b0;

  // Notes on the sheet:
  //   0-9
  //   Botom
  //   Fliped For Some Reason?
  //   Top
endmodule

module Single_Reset_register (
  input  Reset,
  input  Sets__4_bit,
  input  in_3,
  input  in_4,
  input  in_5,
  output out_6,
  output out_7,
  output out_8,
  output out_9
);

  wire and_1_out, and_2_out, and_3_out, and_4_out;

  and and_1 (and_1_out, 1'b0, Reset);
  and and_2 (and_2_out, 1'b0, Reset);
  and and_3 (and_3_out, 1'b0, Reset);
  and and_4 (and_4_out, 1'b0, Reset);
  _1_Bit_Holder u_1_bit_holder_1 (.Set(Sets__4_bit), .Reset(and_1_out), .out_3(out_6));
  _1_Bit_Holder u_1_bit_holder_2 (.Set(in_3), .Reset(and_2_out), .out_3(out_7));
  _1_Bit_Holder u_1_bit_holder_3 (.Set(in_4), .Reset(and_3_out), .out_3(out_8));
  _1_Bit_Holder u_1_bit_holder_4 (.Set(in_5), .Reset(and_4_out), .out_3(out_9));

  // Notes on the sheet:
  //   Top (1) down (8)
endmodule

module Stable_1_bit_Holder (
  input  in_1,
  input  in_2,
  input  in_3,
  input  in_4,
  input  Set,
  input  Reset,
  input  in_7,
  input  in_8,
  input  in_9,
  input  in_10,
  output out_11
);

  T_Flip_Flop t_ff_1 (.T(in_7), .preset(in_9), .reset(in_10), .en(in_8));  // open: clk, Q, Qn
  RAM #(.addrWidth(4), .dataWidth(4)) ram_1 (.addr({in_4, in_3, in_2, in_1}));  // open: data, sel, clk, ld, clr
endmodule
